// Logisim project CPU.circ as structural Verilog: 4 circuits, main circuit main
module main (
  input  _1,
  input  _2,
  input  _3,
  input  _4,
  input  _5,
  input  _6,
  input  _7,
  input  _8,
  input  _9,
  input  _0,
  input  [7:0] in_11,
  input  in_12,
  input  [3:0] in_13,
  input  in_14,
  output out_15,
  output out_16,
  output out_17,
  output out_18,
  output Overflow,
  output is_Zero
);

  wire and_1_out, and_2_out, and_3_out, and_4_out, and_5_out, and_6_out, and_7_out, and_8_out, and_9_out,
       and_10_out, and_11_out, and_12_out, and_14_out, and_15_out, and_16_out, and_17_out, and_18_out,
       and_19_out, button_1_out, button_2_out, button_3_out, clock_1_out, gr_input_selector_1_out_29,
       gr_input_selector_1_out_30, gr_input_selector_1_out_31, gr_input_selector_1_out_32,
       gr_input_selector_1_out_33, gr_input_selector_1_out_34, gr_input_selector_1_out_35,
       gr_input_selector_1_out_36, gr_input_selector_2_out_29, gr_input_selector_2_out_30,
       gr_input_selector_2_out_31, gr_input_selector_2_out_32, gr_input_selector_2_out_33,
       gr_input_selector_2_out_34, gr_input_selector_2_out_35, gr_input_selector_2_out_36, ir_1_out_11,
       ir_1_out_12, ir_1_out_13, ir_1_out_14, ir_1_out_15, ir_1_out_16, ir_1_out_17, ir_1_out_18,
       ir_2_out_11, ir_2_out_12, ir_2_out_13, ir_2_out_14, ir_2_out_15, ir_2_out_16, ir_2_out_17,
       ir_2_out_18, ir_3_out_11, ir_3_out_12, ir_3_out_13, ir_3_out_14, ir_3_out_15, ir_3_out_16,
       ir_3_out_17, ir_3_out_18, main_1_out_26, main_1_out_27, main_1_out_28, main_1_out_29, main_1_out_30,
       main_1_out_31, main_1_out_32, main_1_out_33, main_2_out_17, main_2_out_18, main_2_out_19,
       main_2_out_20, main_2_out_21, main_2_out_22, main_2_out_23, main_2_out_24, main_3_out_10,
       main_3_out_11, main_3_out_12, main_3_out_13, main_5_out_10, main_5_out_11, main_5_out_12,
       main_5_out_13, main_5_out_14, main_5_out_15, main_5_out_16, main_6_success, main_8_out_11,
       main_8_out_12, main_8_out_13, main_8_out_14, main_8_out_15, main_8_out_16, main_8_out_17,
       main_8_out_18, main_9_out_10, main_9_out_11, main_9_out_12, main_9_out_13, main_9_out_14,
       main_9_out_15, main_9_out_16, main_9_out_17, main_11_out_17, main_11_out_18, main_11_out_19,
       main_11_out_20, main_11_out_21, main_11_out_22, main_11_out_23, main_11_out_24, not_1_out, not_2_out,
       not_3_out, not_4_out, not_5_out, not_6_out, not_7_out, not_8_out, not_9_out, not_10_out, not_11_out,
       not_12_out, not_13_out, not_14_out, not_15_out, not_16_out, not_17_out, not_18_out, or_1_out,
       register_saves_data_1_p1, register_saves_data_1_p2, register_saves_data_1_p3,
       register_saves_data_1_p4, register_saves_data_1_p5, register_saves_data_1_p6,
       register_saves_data_1_p7, register_saves_data_1_p8, register_saves_data_1_p10,
       store_selector_2_out_19, store_selector_2_out_20, store_selector_2_out_21, store_selector_2_out_22,
       store_selector_2_out_23, store_selector_2_out_24, store_selector_2_out_25, store_selector_2_out_26;
  wire [7:0] main_7_out_21, main_10_out_22, store_selector_1_out_26;

  Clock clock_1 (.out(clock_1_out));
  not not_1 (not_1_out, ir_1_out_11);
  not not_2 (not_2_out, ir_1_out_12);
  and and_1 (and_1_out, not_1_out, not_2_out, ir_1_out_13);
  not not_3 (not_3_out, in_12);
  Button button_1 (.out(button_1_out));
  not not_4 (not_4_out, ir_1_out_11);
  not not_5 (not_5_out, ir_1_out_13);
  and and_2 (and_2_out, not_4_out, ir_1_out_12, not_5_out);
  and and_3 (and_3_out, in_12, clock_1_out);
  and and_4 (and_4_out, not_3_out, clock_1_out);
  not not_6 (not_6_out, ir_1_out_11);
  Button button_2 (.out(button_2_out));
  and and_5 (and_5_out, not_6_out, ir_1_out_12, ir_1_out_13);
  ALU_with_multiplication_main main_1 (
    .mult(and_7_out), .sub(and_6_out), .add(and_5_out), .Clock(clock_1_out), .in_21(button_1_out),
    .in_1(ir_3_out_11), .in_2(ir_3_out_12), .in_3(ir_3_out_13), .in_4(ir_3_out_14), .in_5(ir_3_out_15),
    .in_6(ir_3_out_16), .in_7(ir_3_out_17), .in_8(ir_3_out_18), .in_9(ir_2_out_11), .in_10(ir_2_out_12),
    .in_11(ir_2_out_13), .in_12(ir_2_out_14), .in_13(ir_2_out_15), .in_14(ir_2_out_16), .in_15(ir_2_out_17),
    .in_16(ir_2_out_18), .out_26(main_1_out_26), .out_27(main_1_out_27), .out_28(main_1_out_28),
    .out_29(main_1_out_29), .out_30(main_1_out_30), .out_31(main_1_out_31), .out_32(main_1_out_32),
    .out_33(main_1_out_33), .Is_zero(is_Zero), .out_23(Overflow));  // open: out_24, out_25
  not not_7 (not_7_out, ir_1_out_12);
  and and_6 (and_6_out, ir_1_out_11, not_7_out, not_8_out);
  and and_7 (and_7_out, and_5_out, ir_1_out_16);
  not not_8 (not_8_out, ir_1_out_13);
  Data_Cache_main main_2 (
    .in_1(main_3_out_13), .address(main_3_out_12), .in_3(main_3_out_11), .in_4(main_3_out_10), .read(1'b1),
    .write(in_12), .in_7(in_11[0]), .in_8(in_11[1]), .in_9(in_11[2]), .data(in_11[3]), .in_11(in_11[4]),
    .in_12(in_11[5]), .in_13(in_11[6]), .in_14(in_11[7]), .Clock(and_3_out), .Zero(button_2_out),
    .out_17(main_2_out_17), .out_18(main_2_out_18), .out_19(main_2_out_19), .out_20(main_2_out_20),
    .out_21(main_2_out_21), .out_22(main_2_out_22), .out_23(main_2_out_23), .out_24(main_2_out_24));
  IR ir_1 (
    .Clock(and_4_out), .in_1(main_2_out_24), .in_2(main_2_out_23), .in_3(main_2_out_22),
    .in_4(main_2_out_21), .in_5(main_2_out_20), .in_6(main_2_out_19), .in_7(main_2_out_18),
    .in_8(main_2_out_17), .out_11(ir_1_out_11), .out_12(ir_1_out_12), .out_13(ir_1_out_13),
    .out_14(ir_1_out_14), .out_15(ir_1_out_15), .out_16(ir_1_out_16), .out_17(ir_1_out_17),
    .out_18(ir_1_out_18), .ON_OFF(button_1_out));
  not not_9 (not_9_out, ir_1_out_12);
  and and_8 (and_8_out, ir_1_out_11, not_9_out, ir_1_out_13);
  helper_main main_3 (
    .in_9(in_14), .in_4(in_13[3]), .in_1(in_13[2]), .in_2(in_13[1]), .in_5(in_13[0]), .in_6(out_15),
    .in_7(out_16), .in_8(out_17), .in_3(out_18), .out_10(main_3_out_10), .out_11(main_3_out_11),
    .out_12(main_3_out_12), .out_13(main_3_out_13));
  not not_10 (not_10_out, ir_1_out_13);
  and and_9 (and_9_out, ir_1_out_11, ir_1_out_12, not_10_out);
  IR ir_2 (
    .Clock(or_1_out), .in_1(main_10_out_22[0]), .in_2(main_10_out_22[1]), .in_3(main_10_out_22[2]),
    .in_4(main_10_out_22[3]), .in_5(main_10_out_22[4]), .in_6(main_10_out_22[5]), .in_7(main_10_out_22[6]),
    .in_8(main_10_out_22[7]), .out_11(ir_2_out_11), .out_12(ir_2_out_12), .out_13(ir_2_out_13),
    .out_14(ir_2_out_14), .out_15(ir_2_out_15), .out_16(ir_2_out_16), .out_17(ir_2_out_17),
    .out_18(ir_2_out_18), .ON_OFF(button_1_out));
  IR ir_3 (
    .Clock(or_1_out), .in_1(main_7_out_21[7]), .in_2(main_7_out_21[6]), .in_3(main_7_out_21[5]),
    .in_4(main_7_out_21[4]), .in_5(main_7_out_21[3]), .in_6(main_7_out_21[2]), .in_7(main_7_out_21[1]),
    .in_8(main_7_out_21[0]), .out_11(ir_3_out_11), .out_12(ir_3_out_12), .out_13(ir_3_out_13),
    .out_14(ir_3_out_14), .out_15(ir_3_out_15), .out_16(ir_3_out_16), .out_17(ir_3_out_17),
    .out_18(ir_3_out_18), .ON_OFF(button_1_out));
  Program_Counter_main main_4 (
    .in_1(register_saves_data_1_p1), .in_2(register_saves_data_1_p3), .in_3(register_saves_data_1_p5),
    .in_4(register_saves_data_1_p7), .clock(clock_1_out), .stop(and_11_out), .bz_bnz(main_6_success),
    .on_off(button_1_out), .out_9(out_15), .out_10(out_16), .out_11(out_17), .out_12(out_18));
  and and_10 (and_10_out, ir_1_out_11, ir_1_out_12, ir_1_out_13);
  not not_11 (not_11_out, ir_1_out_13);
  not not_12 (not_12_out, ir_1_out_12);
  not not_13 (not_13_out, ir_1_out_11);
  and and_11 (and_11_out, not_13_out, not_12_out, ir_1_out_18, not_11_out);
  or or_1 (or_1_out, and_6_out, and_5_out);
  not not_14 (not_14_out, and_11_out);
  and and_12 (and_12_out, not_14_out, clock_1_out);
  _7_Segment_Display u_7_segment_display_1 (
    .g(main_5_out_11), .f(main_5_out_12), .a(main_5_out_13), .b(main_5_out_14), .e(main_5_out_15),
    .d(main_5_out_16), .c(main_5_out_10));  // open: dp
  Store_Selector store_selector_1 (
    .of_GP(ir_1_out_14), .in_1(main_7_out_21[7]), .in_2(main_7_out_21[6]), .in_3(main_7_out_21[5]),
    .R0(main_7_out_21[4]), .in_5(main_7_out_21[3]), .in_6(main_7_out_21[2]), .in_7(main_7_out_21[1]),
    .in_8(main_7_out_21[0]), .in_9(main_10_out_22[0]), .in_10(main_10_out_22[1]), .in_11(main_10_out_22[2]),
    .R1(main_10_out_22[3]), .in_13(main_10_out_22[4]), .in_14(main_10_out_22[5]), .in_15(main_10_out_22[6]),
    .in_16(main_10_out_22[7]), .out_19(store_selector_1_out_26[7]), .out_20(store_selector_1_out_26[6]),
    .out_21(store_selector_1_out_26[5]), .out_22(store_selector_1_out_26[4]),
    .out_23(store_selector_1_out_26[3]), .out_24(store_selector_1_out_26[2]),
    .out_25(store_selector_1_out_26[1]), .out_26(store_selector_1_out_26[0]), .in_18(and_8_out));
  // register_saves_data register_saves_data_1: pin names not known; wires that end beside it: register_saves_data_1_p1, register_saves_data_1_p2, register_saves_data_1_p3, register_saves_data_1_p4, register_saves_data_1_p5, register_saves_data_1_p6, register_saves_data_1_p7, register_saves_data_1_p8, button_1_out, register_saves_data_1_p10
  _7_Segment_main main_5 (
    .in_9(and_12_out), .in_1(store_selector_1_out_26[0]), .in_2(store_selector_1_out_26[1]),
    .in_3(store_selector_1_out_26[2]), .in_4(store_selector_1_out_26[3]), .in_5(store_selector_1_out_26[4]),
    .in_6(store_selector_1_out_26[5]), .in_7(store_selector_1_out_26[6]), .in_8(store_selector_1_out_26[7]),
    .out_11(main_5_out_11), .out_12(main_5_out_12), .out_13(main_5_out_13), .out_14(main_5_out_14),
    .out_15(main_5_out_15), .out_16(main_5_out_16), .out_10(main_5_out_10));
  and and_13 (register_saves_data_1_p10, clock_1_out, main_6_success);
  bz_bnz_analyzer_main main_6 (
    .in_1(and_10_out), ._1_bnz(ir_1_out_14), .in_3(main_7_out_21[0]), .in_4(main_7_out_21[1]),
    .in_5(main_7_out_21[2]), .in_6(main_7_out_21[3]), .in_7(main_7_out_21[4]), .in_8(main_7_out_21[5]),
    .in_9(main_7_out_21[6]), .in_10(main_7_out_21[7]), .in_11(ir_1_out_15), .in_12(ir_1_out_16),
    .in_13(ir_1_out_17), .in_14(ir_1_out_18), .out_15(register_saves_data_1_p8),
    .out_16(register_saves_data_1_p6), .out_17(register_saves_data_1_p4), .out_18(register_saves_data_1_p2),
    .success(main_6_success));
  not not_15 (not_15_out, ir_1_out_14);
  and and_14 (and_14_out, not_15_out, clock_1_out);
  General_Purpose_Register_main main_7 (
    .in_7(and_16_out), .clock(and_14_out), .in_12(not_17_out), .On_Off(button_1_out),
    .in_8(gr_input_selector_1_out_29), .in_9(gr_input_selector_1_out_30), .in_1(gr_input_selector_1_out_31),
    .in_2(gr_input_selector_1_out_32), .in_3(gr_input_selector_1_out_33), .in_4(gr_input_selector_1_out_34),
    .in_5(gr_input_selector_1_out_35), .in_6(gr_input_selector_1_out_36), .out_22(main_7_out_21[7]),
    .out_23(main_7_out_21[6]), .out_16(main_7_out_21[5]), .out_17(main_7_out_21[4]),
    .out_18(main_7_out_21[3]), .out_19(main_7_out_21[2]), .out_20(main_7_out_21[1]),
    .out_21(main_7_out_21[0]), .load(and_1_out), .ALU(and_15_out), .read(and_9_out));
  and and_15 (and_15_out, not_16_out, or_1_out);
  not not_16 (not_16_out, ir_1_out_14);
  not not_17 (not_17_out, ir_1_out_14);
  not not_18 (not_18_out, ir_1_out_15);
  and and_16 (and_16_out, or_1_out, not_18_out);
  GR_Input_Selector gr_input_selector_1 (
    .ALU_indicator(or_1_out), .Cache_Indicator(and_1_out), .in_27(and_9_out), .in_1(main_1_out_26),
    .in_2(main_1_out_27), .Result_from_ALU(main_1_out_28), .in_4(main_1_out_29), .in_5(main_1_out_30),
    .in_6(main_1_out_31), .in_7(main_1_out_32), .in_8(main_1_out_33), .in_9(main_11_out_24),
    .in_10(main_11_out_23), .in_11(main_11_out_22), .Reult_from_Cache(main_11_out_21),
    .in_13(main_11_out_20), .in_14(main_11_out_19), .in_15(main_11_out_18), .in_16(main_11_out_17),
    .in_17(main_9_out_10), .in_18(main_9_out_11), .in_19(main_9_out_12), .in_20(main_9_out_13),
    .in_21(main_9_out_14), .in_22(main_9_out_15), .in_23(main_9_out_16), .in_24(main_9_out_17),
    .out_29(gr_input_selector_1_out_29), .out_30(gr_input_selector_1_out_30),
    .out_31(gr_input_selector_1_out_31), .out_32(gr_input_selector_1_out_32),
    .out_33(gr_input_selector_1_out_33), .out_34(gr_input_selector_1_out_34),
    .out_35(gr_input_selector_1_out_35), .out_36(gr_input_selector_1_out_36), .in_28(not_15_out));
  Button button_3 (.out(button_3_out));
  Input_Reader_main main_8 (
    ._1(_1), ._2(_2), ._3(_3), ._4(_4), ._5(_5), ._6(_6), ._7(_7), ._8(_8), ._9(_9), ._0(_0),
    .out_15(main_8_out_15), .out_16(main_8_out_16), .out_17(main_8_out_17), .out_18(main_8_out_18),
    .out_11(main_8_out_11), .out_12(main_8_out_12), .out_13(main_8_out_13), .out_14(main_8_out_14));
  _8_Bit_Register_main main_9 (
    .Clock(button_3_out), .in_1(main_8_out_15), .in_2(main_8_out_16), .in_3(main_8_out_17),
    .in_4(main_8_out_18), .in_5(main_8_out_11), .in_6(main_8_out_12), .in_7(main_8_out_13),
    .in_8(main_8_out_14), .out_10(main_9_out_10), .out_11(main_9_out_11), .out_12(main_9_out_12),
    .out_13(main_9_out_13), .out_14(main_9_out_14), .out_15(main_9_out_15), .out_16(main_9_out_16),
    .out_17(main_9_out_17));
  and and_17 (and_17_out, clock_1_out, ir_1_out_14);
  General_Purpose_Register_main main_10 (
    .in_7(and_19_out), .clock(and_17_out), .in_12(ir_1_out_14), .On_Off(button_1_out),
    .in_8(gr_input_selector_2_out_29), .in_9(gr_input_selector_2_out_30), .in_1(gr_input_selector_2_out_31),
    .in_2(gr_input_selector_2_out_32), .in_3(gr_input_selector_2_out_33), .in_4(gr_input_selector_2_out_34),
    .in_5(gr_input_selector_2_out_35), .in_6(gr_input_selector_2_out_36), .out_22(main_10_out_22[0]),
    .out_23(main_10_out_22[1]), .out_16(main_10_out_22[2]), .out_17(main_10_out_22[3]),
    .out_18(main_10_out_22[4]), .out_19(main_10_out_22[5]), .out_20(main_10_out_22[6]),
    .out_21(main_10_out_22[7]), .load(and_1_out), .ALU(and_18_out), .read(and_9_out));
  and and_18 (and_18_out, ir_1_out_14, or_1_out);
  and and_19 (and_19_out, or_1_out, ir_1_out_15);
  GR_Input_Selector gr_input_selector_2 (
    .ALU_indicator(or_1_out), .Cache_Indicator(and_1_out), .in_27(and_9_out), .in_1(main_1_out_26),
    .in_2(main_1_out_27), .Result_from_ALU(main_1_out_28), .in_4(main_1_out_29), .in_5(main_1_out_30),
    .in_6(main_1_out_31), .in_7(main_1_out_32), .in_8(main_1_out_33), .in_9(main_11_out_24),
    .in_10(main_11_out_23), .in_11(main_11_out_22), .Reult_from_Cache(main_11_out_21),
    .in_13(main_11_out_20), .in_14(main_11_out_19), .in_15(main_11_out_18), .in_16(main_11_out_17),
    .in_17(main_9_out_10), .in_18(main_9_out_11), .in_19(main_9_out_12), .in_20(main_9_out_13),
    .in_21(main_9_out_14), .in_22(main_9_out_15), .in_23(main_9_out_16), .in_24(main_9_out_17),
    .out_29(gr_input_selector_2_out_29), .out_30(gr_input_selector_2_out_30),
    .out_31(gr_input_selector_2_out_31), .out_32(gr_input_selector_2_out_32),
    .out_33(gr_input_selector_2_out_33), .out_34(gr_input_selector_2_out_34),
    .out_35(gr_input_selector_2_out_35), .out_36(gr_input_selector_2_out_36), .in_28(ir_1_out_14));
  Store_Selector store_selector_2 (
    .of_GP(ir_1_out_14), .in_1(main_7_out_21[0]), .in_2(main_7_out_21[1]), .in_3(main_7_out_21[2]),
    .R0(main_7_out_21[3]), .in_5(main_7_out_21[4]), .in_6(main_7_out_21[5]), .in_7(main_7_out_21[6]),
    .in_8(main_7_out_21[7]), .in_9(main_10_out_22[7]), .in_10(main_10_out_22[6]), .in_11(main_10_out_22[5]),
    .R1(main_10_out_22[4]), .in_13(main_10_out_22[3]), .in_14(main_10_out_22[2]), .in_15(main_10_out_22[1]),
    .in_16(main_10_out_22[0]), .out_19(store_selector_2_out_19), .out_20(store_selector_2_out_20),
    .out_21(store_selector_2_out_21), .out_22(store_selector_2_out_22), .out_23(store_selector_2_out_23),
    .out_24(store_selector_2_out_24), .out_25(store_selector_2_out_25), .out_26(store_selector_2_out_26),
    .in_18(and_2_out));
  Data_Cache_main main_11 (
    .in_1(ir_1_out_18), .address(ir_1_out_17), .in_3(ir_1_out_16), .in_4(ir_1_out_15), .read(and_1_out),
    .write(and_2_out), .in_7(store_selector_2_out_26), .in_8(store_selector_2_out_25),
    .in_9(store_selector_2_out_24), .data(store_selector_2_out_23), .in_11(store_selector_2_out_22),
    .in_12(store_selector_2_out_21), .in_13(store_selector_2_out_20), .in_14(store_selector_2_out_19),
    .Clock(clock_1_out), .Zero(button_1_out), .out_17(main_11_out_17), .out_18(main_11_out_18),
    .out_19(main_11_out_19), .out_20(main_11_out_20), .out_21(main_11_out_21), .out_22(main_11_out_22),
    .out_23(main_11_out_23), .out_24(main_11_out_24));

  // Notes on the sheet:
  //   load:001
  //   on/off switch
  //   store:010
  //   add:011
  //   clear all current instructions 
  //   in the instruction cache
  //   always read instructions fom instructions cache
  //   sub:100
  //   mult
  //   ALU
  //   instruction Cache
  //   input instructions
  //   print:101
  //   IR
  //   read:110
  //   write new instructions into instruction cache 
  //   branch:111
  //   PC
  //   stop:000
  //   right register of ALU, always take input from R1
  //   left register of ALU, always take input from R0
  //   ouput 
  //   beq
  //   fourth bit
  //   R0
  //   fIfthbit
  //   SAVE
  //   second bit is only used for GP for add and sub
  //   keypad
  //   sixth bit
  //   General Purpose Register
  //   convrter
  //   seventh bit
  //   R1
  //   eighth bit
  //   Data Cache
endmodule

module Store_Selector (
  input  in_1,
  input  in_2,
  input  in_3,
  input  R0,
  input  in_5,
  input  in_6,
  input  in_7,
  input  in_8,
  input  in_9,
  input  in_10,
  input  in_11,
  input  R1,
  input  in_13,
  input  in_14,
  input  in_15,
  input  in_16,
  input  of_GP,
  input  in_18,
  output out_19,
  output out_20,
  output out_21,
  output out_22,
  output out_23,
  output out_24,
  output out_25,
  output out_26
);

  wire and_1_out, and_2_out, and_3_out, and_4_out, and_5_out, and_6_out, and_7_out, and_8_out, and_9_out,
       and_10_out, and_11_out, and_12_out, and_13_out, and_14_out, and_15_out, and_16_out, not_1_out;

  not not_1 (not_1_out, of_GP);
  and and_1 (and_1_out, not_1_out, in_18, in_8);
  or or_1 (out_19, and_1_out, and_2_out);
  and and_2 (and_2_out, of_GP, in_18, in_16);
  and and_3 (and_3_out, not_1_out, in_7, in_18);
  and and_4 (and_4_out, of_GP, in_18, in_15);
  or or_2 (out_20, and_3_out, and_4_out);
  and and_5 (and_5_out, not_1_out, in_6, in_18);
  and and_6 (and_6_out, of_GP, in_18, in_14);
  or or_3 (out_21, and_5_out, and_6_out);
  and and_7 (and_7_out, not_1_out, in_5, in_18);
  and and_8 (and_8_out, of_GP, in_18, in_13);
  or or_4 (out_22, and_7_out, and_8_out);
  and and_9 (and_9_out, not_1_out, R0, in_18);
  or or_5 (out_23, and_9_out, and_10_out);
  and and_10 (and_10_out, of_GP, in_18, R1);
  and and_11 (and_11_out, not_1_out, in_3, in_18);
  or or_6 (out_24, and_11_out, and_12_out);
  and and_12 (and_12_out, of_GP, in_18, in_11);
  and and_13 (and_13_out, not_1_out, in_2, in_18);
  or or_7 (out_25, and_13_out, and_14_out);
  and and_14 (and_14_out, of_GP, in_18, in_10);
  and and_15 (and_15_out, of_GP, in_18, in_9);
  and and_16 (and_16_out, not_1_out, in_1, in_18);
  or or_8 (out_26, and_16_out, and_15_out);

  // Notes on the sheet:
  //   R1 Indicator
  //   R0 Indicator
  //   is store activated
endmodule

module GR_Input_Selector (
  input  in_1,
  input  in_2,
  input  Result_from_ALU,
  input  in_4,
  input  in_5,
  input  in_6,
  input  in_7,
  input  in_8,
  input  in_9,
  input  in_10,
  input  in_11,
  input  Reult_from_Cache,
  input  in_13,
  input  in_14,
  input  in_15,
  input  in_16,
  input  in_17,
  input  in_18,
  input  in_19,
  input  in_20,
  input  in_21,
  input  in_22,
  input  in_23,
  input  in_24,
  input  ALU_indicator,
  input  Cache_Indicator,
  input  in_27,
  input  in_28,
  output out_29,
  output out_30,
  output out_31,
  output out_32,
  output out_33,
  output out_34,
  output out_35,
  output out_36
);

  wire and_1_out, and_2_out, and_4_out, and_5_out, and_6_out, and_8_out, and_9_out, and_10_out, and_12_out,
       and_13_out, and_14_out, and_16_out, and_17_out, and_18_out, and_19_out, and_21_out, and_22_out,
       and_24_out, and_25_out, and_26_out, and_28_out, and_29_out, and_30_out, and_32_out, or_1_out,
       or_2_out, or_3_out, or_4_out, or_5_out, or_6_out, or_7_out, or_8_out;

  and and_1 (and_1_out, ALU_indicator, in_1);
  and and_2 (and_2_out, Cache_Indicator, in_9);
  or or_1 (or_1_out, and_1_out, and_2_out, and_4_out);
  and and_3 (out_29, or_1_out, in_28);
  and and_4 (and_4_out, in_27, in_17);
  and and_5 (and_5_out, ALU_indicator, in_2);
  and and_6 (and_6_out, Cache_Indicator, in_10);
  or or_2 (or_2_out, and_5_out, and_6_out, and_8_out);
  and and_7 (out_30, or_2_out, in_28);
  and and_8 (and_8_out, in_27, in_18);
  and and_9 (and_9_out, ALU_indicator, Result_from_ALU);
  and and_10 (and_10_out, Cache_Indicator, in_11);
  or or_3 (or_3_out, and_9_out, and_10_out, and_12_out);
  and and_11 (out_31, or_3_out, in_28);
  and and_12 (and_12_out, in_27, in_19);
  and and_13 (and_13_out, ALU_indicator, in_4);
  and and_14 (and_14_out, Cache_Indicator, Reult_from_Cache);
  or or_4 (or_4_out, and_13_out, and_14_out, and_16_out);
  and and_15 (out_32, or_4_out, in_28);
  and and_16 (and_16_out, in_27, in_20);
  and and_17 (and_17_out, Cache_Indicator, in_13);
  and and_18 (and_18_out, ALU_indicator, in_5);
  or or_5 (or_5_out, and_18_out, and_17_out, and_19_out);
  and and_19 (and_19_out, in_27, in_21);
  and and_20 (out_33, or_5_out, in_28);
  and and_21 (and_21_out, ALU_indicator, in_6);
  and and_22 (and_22_out, Cache_Indicator, in_14);
  or or_6 (or_6_out, and_21_out, and_22_out, and_24_out);
  and and_23 (out_34, or_6_out, in_28);
  and and_24 (and_24_out, in_27, in_22);
  and and_25 (and_25_out, ALU_indicator, in_7);
  and and_26 (and_26_out, Cache_Indicator, in_15);
  or or_7 (or_7_out, and_25_out, and_26_out, and_28_out);
  and and_27 (out_35, or_7_out, in_28);
  and and_28 (and_28_out, in_27, in_23);
  and and_29 (and_29_out, ALU_indicator, in_8);
  and and_30 (and_30_out, Cache_Indicator, in_16);
  or or_8 (or_8_out, and_29_out, and_30_out, and_32_out);
  and and_31 (out_36, or_8_out, in_28);
  and and_32 (and_32_out, in_27, in_24);

  // Notes on the sheet:
  //   Keyboard Indicator
  //   Reult from Keyboard
  //   number of register
endmodule

module IR (
  input  in_1,
  input  in_2,
  input  in_3,
  input  in_4,
  input  in_5,
  input  in_6,
  input  in_7,
  input  in_8,
  input  Clock,
  input  ON_OFF,
  output out_11,
  output out_12,
  output out_13,
  output out_14,
  output out_15,
  output out_16,
  output out_17,
  output out_18
);

  D_Flip_Flop d_ff_1 (.clk(Clock), .D(in_1), .Q(out_11), .reset(ON_OFF));  // open: Qn, preset, en
  D_Flip_Flop d_ff_2 (.clk(Clock), .D(in_2), .Q(out_12), .reset(ON_OFF));  // open: Qn, preset, en
  D_Flip_Flop d_ff_3 (.clk(Clock), .D(in_3), .Q(out_13), .reset(ON_OFF));  // open: Qn, preset, en
  D_Flip_Flop d_ff_4 (.clk(Clock), .D(in_4), .Q(out_14), .reset(ON_OFF));  // open: Qn, preset, en
  D_Flip_Flop d_ff_5 (.clk(Clock), .D(in_5), .Q(out_15), .reset(ON_OFF));  // open: Qn, preset, en
  D_Flip_Flop d_ff_6 (.clk(Clock), .D(in_6), .Q(out_16), .reset(ON_OFF));  // open: Qn, preset, en
  D_Flip_Flop d_ff_7 (.clk(Clock), .D(in_7), .Q(out_17), .reset(ON_OFF));  // open: Qn, preset, en
  D_Flip_Flop d_ff_8 (.clk(Clock), .D(in_8), .Q(out_18), .reset(ON_OFF));  // open: Qn, preset, en
endmodule
