// Logisim project 16 Byte.circ as structural Verilog: 8 circuits, main circuit RE Latch
module BYTE (
  input  in_1,
  input  in_2,
  input  in_3,
  input  [7:0] in_4,
  output out_5,
  output out_6,
  output out_7,
  output out_8,
  output out_9,
  output out_10,
  output out_11,
  output out_12
);

  wire and_1_out, and_2_out, and_3_out, and_4_out, and_5_out, and_6_out, and_7_out, and_8_out, and_9_out,
       and_10_out, and_11_out, and_12_out, and_13_out, and_14_out, and_15_out, and_16_out, and_17_out,
       not_1_out, not_2_out, not_3_out, not_4_out, not_5_out, not_6_out, not_7_out, not_8_out,
       re_latch_1_out_3, re_latch_2_out_3, re_latch_3_out_3, re_latch_4_out_3, re_latch_5_out_3,
       re_latch_6_out_3, re_latch_7_out_3, re_latch_8_out_3;

  and and_1 (and_1_out, in_2, in_3);
  and and_2 (and_2_out, and_1_out, in_4[0]);
  and and_3 (and_3_out, and_1_out, in_4[1]);
  and and_4 (and_4_out, and_1_out, in_4[2]);
  and and_5 (and_5_out, and_1_out, in_4[3]);
  and and_6 (and_6_out, and_1_out, in_4[5]);
  and and_7 (and_7_out, and_1_out, in_4[6]);
  and and_8 (and_8_out, and_1_out, in_4[7]);
  not not_1 (not_1_out, in_4[0]);
  not not_2 (not_2_out, in_4[2]);
  not not_3 (not_3_out, in_4[3]);
  and and_9 (and_9_out, and_1_out, in_4[4]);
  not not_4 (not_4_out, in_4[4]);
  not not_5 (not_5_out, in_4[5]);
  not not_6 (not_6_out, in_4[6]);
  not not_7 (not_7_out, in_4[7]);
  and and_10 (and_10_out, and_1_out, not_1_out);
  and and_11 (and_11_out, and_1_out, not_8_out);
  not not_8 (not_8_out, in_4[1]);
  and and_12 (and_12_out, and_1_out, not_2_out);
  and and_13 (and_13_out, and_1_out, not_3_out);
  and and_14 (and_14_out, and_1_out, not_4_out);
  and and_15 (and_15_out, and_1_out, not_5_out);
  and and_16 (and_16_out, and_1_out, not_6_out);
  and and_17 (and_17_out, and_1_out, not_7_out);
  RE_Latch re_latch_1 (.in_1(and_10_out), .in_2(and_2_out), .out_3(re_latch_1_out_3));  // open: out_4
  RE_Latch re_latch_2 (.in_1(and_11_out), .in_2(and_3_out), .out_3(re_latch_2_out_3));  // open: out_4
  RE_Latch re_latch_3 (.in_1(and_12_out), .in_2(and_4_out), .out_3(re_latch_3_out_3));  // open: out_4
  RE_Latch re_latch_4 (.in_1(and_13_out), .in_2(and_5_out), .out_3(re_latch_4_out_3));  // open: out_4
  RE_Latch re_latch_5 (.in_1(and_14_out), .in_2(and_9_out), .out_3(re_latch_5_out_3));  // open: out_4
  RE_Latch re_latch_6 (.in_1(and_15_out), .in_2(and_6_out), .out_3(re_latch_6_out_3));  // open: out_4
  RE_Latch re_latch_7 (.in_1(and_16_out), .in_2(and_7_out), .out_3(re_latch_7_out_3));  // open: out_4
  RE_Latch re_latch_8 (.in_1(and_17_out), .in_2(and_8_out), .out_3(re_latch_8_out_3));  // open: out_4
  and and_18 (out_5, in_1, re_latch_1_out_3);
  and and_19 (out_6, in_1, re_latch_2_out_3);
  and and_20 (out_7, in_1, re_latch_3_out_3);
  and and_21 (out_8, in_1, re_latch_4_out_3);
  and and_22 (out_9, in_1, re_latch_5_out_3);
  and and_23 (out_10, in_1, re_latch_6_out_3);
  and and_24 (out_11, in_1, re_latch_7_out_3);
  and and_25 (out_12, in_1, re_latch_8_out_3);
endmodule

module RE_Latch (
  input  in_1,
  input  in_2,
  output out_3,
  output out_4
);

  nor nor_1 (out_3, in_1, out_4);
  nor nor_2 (out_4, out_3, in_2);
endmodule

module main (
  input  in_1,
  input  address,
  input  in_3,
  input  in_4,
  input  read,
  input  write,
  input  in_7,
  input  in_8,
  input  in_9,
  input  data,
  input  in_11,
  input  in_12,
  input  in_13,
  input  in_14,
  output out_15,
  output out_16,
  output out_17,
  output out_18,
  output out_19,
  output out_20,
  output out_21,
  output out_22
);

  wire address_director_1_out_2, address_director_1_out_3, address_director_1_out_4,
       address_director_1_out_5, address_director_1_out_6, address_director_1_out_7,
       address_director_1_out_8, address_director_1_out_9, address_director_1_out_10,
       address_director_1_out_11, address_director_1_out_12, address_director_1_out_13,
       address_director_1_out_14, address_director_1_out_15, address_director_1_out_16,
       address_director_1_out_17;
  wire [7:0] n4_bytes_1_out_8, n4_bytes_1_out_9, n4_bytes_1_out_10, n4_bytes_1_out_11, n4_bytes_2_out_8,
       n4_bytes_2_out_9, n4_bytes_2_out_10, n4_bytes_2_out_11, n4_bytes_3_out_8, n4_bytes_3_out_9,
       n4_bytes_3_out_10, n4_bytes_3_out_11, n4_bytes_4_out_8, n4_bytes_4_out_9, n4_bytes_4_out_10,
       n4_bytes_4_out_11;

  Address_Director address_director_1 (
    .in_1({in_4, in_3, address, in_1}), .out_2(address_director_1_out_2), .out_3(address_director_1_out_3),
    .out_4(address_director_1_out_4), .out_5(address_director_1_out_5), .out_6(address_director_1_out_6),
    .out_7(address_director_1_out_7), .out_8(address_director_1_out_8), .out_9(address_director_1_out_9),
    .out_10(address_director_1_out_10), .out_11(address_director_1_out_11),
    .out_12(address_director_1_out_12), .out_13(address_director_1_out_13),
    .out_14(address_director_1_out_14), .out_15(address_director_1_out_15),
    .out_16(address_director_1_out_16), .out_17(address_director_1_out_17));
  _4_bytes u_4_bytes_1 (
    .W(write), .AddCheck1(address_director_1_out_2), .AddCheck2(address_director_1_out_3),
    .AddCheck3(address_director_1_out_4), .AddCheck4(address_director_1_out_5),
    .in_6({in_14, in_13, in_12, in_11, data, in_9, in_8, in_7}), .R(read), .out_8(n4_bytes_1_out_8),
    .out_9(n4_bytes_1_out_9), .out_10(n4_bytes_1_out_10), .out_11(n4_bytes_1_out_11));
  _4_bytes u_4_bytes_2 (
    .W(write), .AddCheck1(address_director_1_out_6), .AddCheck2(address_director_1_out_7),
    .AddCheck3(address_director_1_out_8), .AddCheck4(address_director_1_out_9),
    .in_6({in_14, in_13, in_12, in_11, data, in_9, in_8, in_7}), .R(read), .out_8(n4_bytes_2_out_8),
    .out_9(n4_bytes_2_out_9), .out_10(n4_bytes_2_out_10), .out_11(n4_bytes_2_out_11));
  _4_bytes u_4_bytes_3 (
    .W(write), .AddCheck1(address_director_1_out_10), .AddCheck2(address_director_1_out_11),
    .AddCheck3(address_director_1_out_12), .AddCheck4(address_director_1_out_13),
    .in_6({in_14, in_13, in_12, in_11, data, in_9, in_8, in_7}), .R(read), .out_8(n4_bytes_3_out_8),
    .out_9(n4_bytes_3_out_9), .out_10(n4_bytes_3_out_10), .out_11(n4_bytes_3_out_11));
  _4_bytes u_4_bytes_4 (
    .W(write), .AddCheck1(address_director_1_out_14), .AddCheck2(address_director_1_out_15),
    .AddCheck3(address_director_1_out_16), .AddCheck4(address_director_1_out_17),
    .in_6({in_14, in_13, in_12, in_11, data, in_9, in_8, in_7}), .R(read), .out_8(n4_bytes_4_out_8),
    .out_9(n4_bytes_4_out_9), .out_10(n4_bytes_4_out_10), .out_11(n4_bytes_4_out_11));
  assign {out_15, out_16, out_17, out_18, out_19, out_20, out_21, out_22} = n4_bytes_1_out_8 | n4_bytes_1_out_9 | n4_bytes_1_out_10 | n4_bytes_1_out_11 | n4_bytes_2_out_8 | n4_bytes_2_out_9 | n4_bytes_2_out_10 | n4_bytes_2_out_11 | n4_bytes_3_out_8 | n4_bytes_3_out_9 | n4_bytes_3_out_10 | n4_bytes_3_out_11 | n4_bytes_4_out_8 | n4_bytes_4_out_9 | n4_bytes_4_out_10 | n4_bytes_4_out_11;  // OR_Gate or_1, 8 bits wide
endmodule

module ADD_Check (
  input  in_1,
  input  in_2,
  input  in_3,
  output out_4,
  output out_5,
  output out_6,
  output out_7
);

  wire and_1_out, and_2_out, and_3_out, not_1_out, not_2_out, not_3_out, not_4_out;

  and and_1 (and_1_out, in_1, in_3);
  and and_2 (and_2_out, in_2, in_3);
  not not_1 (not_1_out, and_1_out);
  not not_2 (not_2_out, and_2_out);
  not not_3 (not_3_out, and_2_out);
  not not_4 (not_4_out, and_1_out);
  and and_3 (and_3_out, not_1_out, not_2_out);
  and and_4 (out_5, and_1_out, not_3_out);
  and and_5 (out_6, not_4_out, and_2_out);
  and and_6 (out_7, and_1_out, and_2_out);
  and and_7 (out_4, in_3, and_3_out);
endmodule

module _4_nibble_ram (
  input  [6:0] in_1,
  output [3:0] out_2
);

  // main main_1: pin names not known; wires that end beside it: in_1, out_2
endmodule

module Address_Director (
  input  [3:0] in_1,
  output out_2,
  output out_3,
  output out_4,
  output out_5,
  output out_6,
  output out_7,
  output out_8,
  output out_9,
  output out_10,
  output out_11,
  output out_12,
  output out_13,
  output out_14,
  output out_15,
  output out_16,
  output out_17
);

  wire add_check_1_out_4, add_check_1_out_5, add_check_1_out_6, add_check_1_out_7;

  ADD_Check add_check_1 (
    .in_1(in_1[2]), .in_2(in_1[3]), .in_3(1'b1), .out_4(add_check_1_out_4), .out_5(add_check_1_out_5),
    .out_6(add_check_1_out_6), .out_7(add_check_1_out_7));
  ADD_Check add_check_2 (
    .in_1(in_1[0]), .in_2(in_1[1]), .in_3(add_check_1_out_4), .out_4(out_2), .out_5(out_3), .out_6(out_4),
    .out_7(out_5));
  ADD_Check add_check_3 (
    .in_1(in_1[0]), .in_2(in_1[1]), .in_3(add_check_1_out_5), .out_4(out_6), .out_5(out_7), .out_6(out_8),
    .out_7(out_9));
  ADD_Check add_check_4 (
    .in_1(in_1[0]), .in_2(in_1[1]), .in_3(add_check_1_out_6), .out_4(out_10), .out_5(out_11), .out_6(out_12),
    .out_7(out_13));
  ADD_Check add_check_5 (
    .in_1(in_1[0]), .in_2(in_1[1]), .in_3(add_check_1_out_7), .out_4(out_14), .out_5(out_15), .out_6(out_16),
    .out_7(out_17));
endmodule

module _1_bit_to_8_bit (
  input  in_1,
  output [7:0] out_2
);


  assign out_2 = {8{in_1}};
endmodule

module _4_bytes (
  input  W,
  input  AddCheck1,
  input  AddCheck2,
  input  AddCheck3,
  input  AddCheck4,
  input  [7:0] in_6,
  input  R,
  output [7:0] out_8,
  output [7:0] out_9,
  output [7:0] out_10,
  output [7:0] out_11
);

  wire [7:0] byte_1_out_12, byte_2_out_12, byte_3_out_12, byte_4_out_12, n1_bit_to_8_bit_1_out_2,
       n1_bit_to_8_bit_2_out_2, n1_bit_to_8_bit_3_out_2, n1_bit_to_8_bit_4_out_2;

  BYTE byte_1 (
    .in_1(R), .in_2(AddCheck1), .in_3(W), .in_4(in_6), .out_5(byte_1_out_12[7]), .out_6(byte_1_out_12[6]),
    .out_7(byte_1_out_12[5]), .out_8(byte_1_out_12[4]), .out_9(byte_1_out_12[3]), .out_10(byte_1_out_12[2]),
    .out_11(byte_1_out_12[1]), .out_12(byte_1_out_12[0]));
  BYTE byte_2 (
    .in_1(R), .in_2(AddCheck2), .in_3(W), .in_4(in_6), .out_5(byte_2_out_12[7]), .out_6(byte_2_out_12[6]),
    .out_7(byte_2_out_12[5]), .out_8(byte_2_out_12[4]), .out_9(byte_2_out_12[3]), .out_10(byte_2_out_12[2]),
    .out_11(byte_2_out_12[1]), .out_12(byte_2_out_12[0]));
  BYTE byte_3 (
    .in_1(R), .in_2(AddCheck3), .in_3(W), .in_4(in_6), .out_5(byte_3_out_12[7]), .out_6(byte_3_out_12[6]),
    .out_7(byte_3_out_12[5]), .out_8(byte_3_out_12[4]), .out_9(byte_3_out_12[3]), .out_10(byte_3_out_12[2]),
    .out_11(byte_3_out_12[1]), .out_12(byte_3_out_12[0]));
  BYTE byte_4 (
    .in_1(R), .in_2(AddCheck4), .in_3(W), .in_4(in_6), .out_5(byte_4_out_12[7]), .out_6(byte_4_out_12[6]),
    .out_7(byte_4_out_12[5]), .out_8(byte_4_out_12[4]), .out_9(byte_4_out_12[3]), .out_10(byte_4_out_12[2]),
    .out_11(byte_4_out_12[1]), .out_12(byte_4_out_12[0]));
  _1_bit_to_8_bit u_1_bit_to_8_bit_1 (.in_1(AddCheck1), .out_2(n1_bit_to_8_bit_1_out_2));
  _1_bit_to_8_bit u_1_bit_to_8_bit_2 (.in_1(AddCheck2), .out_2(n1_bit_to_8_bit_2_out_2));
  _1_bit_to_8_bit u_1_bit_to_8_bit_3 (.in_1(AddCheck3), .out_2(n1_bit_to_8_bit_3_out_2));
  _1_bit_to_8_bit u_1_bit_to_8_bit_4 (.in_1(AddCheck4), .out_2(n1_bit_to_8_bit_4_out_2));
  assign out_8 = byte_1_out_12 & n1_bit_to_8_bit_1_out_2;  // AND_Gate and_1, 8 bits wide
  assign out_9 = byte_2_out_12 & n1_bit_to_8_bit_2_out_2;  // AND_Gate and_2, 8 bits wide
  assign out_10 = byte_3_out_12 & n1_bit_to_8_bit_3_out_2;  // AND_Gate and_3, 8 bits wide
  assign out_11 = byte_4_out_12 & n1_bit_to_8_bit_4_out_2;  // AND_Gate and_4, 8 bits wide
endmodule
