// Logisim project 7-Segment.circ as structural Verilog: 1 circuit, main circuit main
module main (
  input  in_1,
  input  in_2,
  input  in_3,
  input  in_4,
  input  in_5,
  input  in_6,
  input  in_7,
  input  in_8,
  input  in_9,
  output out_10,
  output out_11,
  output out_12,
  output out_13,
  output out_14,
  output out_15,
  output out_16
);

  wire and_1_out, and_2_out, and_3_out, and_4_out, and_5_out, and_6_out, and_7_out, and_8_out, and_9_out,
       and_10_out, and_11_out, and_12_out, and_13_out, not_1_out, not_2_out, not_3_out, not_4_out, not_5_out,
       not_6_out, not_7_out, not_8_out, not_9_out, not_10_out, not_11_out, not_12_out, not_13_out,
       not_14_out, not_15_out, not_16_out, not_17_out, not_18_out, not_19_out, not_20_out, not_21_out,
       not_22_out, not_23_out, not_24_out, not_25_out, not_26_out, or_1_out, or_2_out, or_3_out, or_4_out,
       or_5_out, or_6_out, or_7_out, or_8_out, or_9_out, or_10_out, or_11_out, or_12_out, or_13_out,
       or_14_out, or_15_out, or_16_out, or_17_out, or_18_out, or_19_out, or_20_out, or_21_out, or_22_out,
       or_23_out, or_24_out;

  _7_Segment_Display u_7_segment_display_1 (
    .g(or_5_out), .f(or_9_out), .a(or_11_out), .b(and_12_out), .e(or_18_out), .d(or_20_out), .c(and_13_out));  // open: dp
  not not_1 (not_1_out, in_8);
  not not_2 (not_2_out, in_7);
  not not_3 (not_3_out, in_7);
  not not_4 (not_4_out, in_8);
  not not_5 (not_5_out, in_8);
  not not_6 (not_6_out, in_7);
  not not_7 (not_7_out, in_7);
  not not_8 (not_8_out, in_8);
  not not_9 (not_9_out, in_8);
  not not_10 (not_10_out, in_7);
  not not_11 (not_11_out, in_7);
  not not_12 (not_12_out, in_6);
  not not_13 (not_13_out, in_5);
  not not_14 (not_14_out, in_6);
  not not_15 (not_15_out, in_5);
  not not_16 (not_16_out, in_6);
  not not_17 (not_17_out, in_5);
  not not_18 (not_18_out, in_6);
  not not_19 (not_19_out, in_5);
  not not_20 (not_20_out, in_5);
  not not_21 (not_21_out, in_5);
  not not_22 (not_22_out, in_5);
  not not_23 (not_23_out, in_5);
  not not_24 (not_24_out, in_6);
  not not_25 (not_25_out, in_6);
  or or_1 (or_1_out, in_7, in_6);
  and and_1 (and_1_out, not_1_out, not_2_out, not_12_out, not_13_out);
  and and_2 (and_2_out, in_8, not_3_out, not_14_out, not_15_out);
  and and_3 (and_3_out, not_4_out, in_7, not_16_out, not_17_out);
  and and_4 (and_4_out, in_8, in_7, not_18_out, not_19_out);
  and and_5 (and_5_out, not_5_out, not_6_out, in_6, not_20_out);
  and and_6 (and_6_out, in_8, not_7_out, in_6, not_21_out);
  and and_7 (and_7_out, not_8_out, in_7, in_6, not_22_out);
  and and_8 (and_8_out, in_8, in_7, in_6, not_23_out);
  and and_9 (and_9_out, not_9_out, not_10_out, not_24_out, in_5);
  and and_10 (and_10_out, in_8, not_11_out, not_25_out, in_5);
  or or_2 (or_2_out, in_4, in_3, in_2, in_1);
  and and_11 (and_11_out, or_1_out, in_5);
  or or_3 (or_3_out, or_2_out, and_11_out);
  not not_26 (not_26_out, or_3_out);
  or or_4 (or_4_out, and_3_out, and_4_out, and_5_out, and_6_out, and_7_out);
  or or_5 (or_5_out, or_4_out, or_6_out);
  or or_6 (or_6_out, and_9_out, and_10_out, or_2_out, and_11_out);
  or or_7 (or_7_out, and_1_out, and_5_out, and_6_out, and_7_out, and_9_out);
  D_Flip_Flop d_ff_1 (.clk(in_9), .D(or_5_out), .Q(out_11));  // open: Qn, preset, en, reset
  or or_8 (or_8_out, and_10_out, or_2_out, and_11_out);
  or or_9 (or_9_out, or_7_out, or_8_out);
  D_Flip_Flop d_ff_2 (.clk(in_9), .D(or_9_out), .Q(out_12));  // open: Qn, preset, en, reset
  or or_10 (or_10_out, and_1_out, and_3_out, and_4_out, and_6_out, and_7_out);
  or or_11 (or_11_out, or_10_out, or_12_out);
  D_Flip_Flop d_ff_3 (.clk(in_9), .D(or_11_out), .Q(out_13));  // open: Qn, preset, en, reset
  or or_12 (or_12_out, and_8_out, and_9_out, and_10_out, or_2_out, and_11_out);
  or or_13 (or_13_out, and_1_out, and_2_out, and_3_out, and_4_out, and_5_out);
  or or_14 (or_14_out, and_8_out, and_9_out, and_10_out);
  or or_15 (or_15_out, or_13_out, or_14_out);
  and and_12 (and_12_out, not_26_out, or_15_out);
  D_Flip_Flop d_ff_4 (.clk(in_9), .D(and_12_out), .Q(out_14));  // open: Qn, preset, en, reset
  or or_16 (or_16_out, and_1_out, and_3_out, and_7_out, and_9_out, or_2_out);
  D_Flip_Flop d_ff_5 (.clk(in_9), .D(or_18_out), .Q(out_15));  // open: Qn, preset, en, reset
  buf or_17 (or_17_out, and_11_out);  // OR_Gate
  or or_18 (or_18_out, or_16_out, or_17_out);
  or or_19 (or_19_out, and_1_out, and_3_out, and_4_out, and_6_out, and_7_out);
  or or_20 (or_20_out, or_19_out, or_21_out);
  D_Flip_Flop d_ff_6 (.clk(in_9), .D(or_20_out), .Q(out_16));  // open: Qn, preset, en, reset
  or or_21 (or_21_out, and_9_out, or_2_out, and_11_out);
  or or_22 (or_22_out, and_1_out, and_2_out, and_4_out, and_5_out, and_6_out);
  or or_23 (or_23_out, and_7_out, and_8_out, and_9_out, and_10_out);
  or or_24 (or_24_out, or_22_out, or_23_out);
  and and_13 (and_13_out, not_26_out, or_24_out);
  D_Flip_Flop d_ff_7 (.clk(in_9), .D(and_13_out), .Q(out_10));  // open: Qn, preset, en, reset

  // Notes on the sheet:
  //   Overflow / Error
  //   The 7-segment here is for internal testing and visibility. The output pins do the same job externally.
  //   This circuit converts an 8-bit binary input into a 7-segment display output. Any output to the display > 9 results in an "E" for overflow/error.
endmodule
