// Logisim project 8-Bit 2's Complement.circ as structural Verilog: 1 circuit, main circuit main
module main (
  input  in_1,
  input  in_2,
  input  in_3,
  input  in_4,
  input  in_5,
  input  in_6,
  input  in_7,
  input  in_8,
  output out_9,
  output out_10,
  output out_11,
  output out_12,
  output out_13,
  output out_14,
  output out_15,
  output out_16
);

  wire half_adder_1_sum, half_adder_3_carry_bit, half_adder_3_sum, half_adder_4_carry_bit,
       half_adder_5_carry_bit, half_adder_5_sum, half_adder_6_carry_bit, half_adder_7_carry_bit,
       half_adder_7_sum, half_adder_8_carry_bit, half_adder_9_carry_bit, half_adder_9_sum,
       half_adder_10_carry_bit, half_adder_11_carry_bit, half_adder_11_sum, half_adder_12_carry_bit,
       half_adder_13_carry_bit, half_adder_13_sum, half_adder_14_carry_bit, half_adder_15_carry_bit,
       not_1_out, not_2_out, not_3_out, not_4_out, not_5_out, not_6_out, not_7_out, not_8_out, not_9_out,
       not_10_out, not_11_out, not_12_out, not_13_out, not_14_out, not_15_out, or_1_out, or_2_out, or_3_out,
       or_4_out, or_5_out, or_6_out;

  not not_1 (not_1_out, in_1);
  not not_2 (not_2_out, 1'b1);
  Half_Adder half_adder_1 (.in_1(not_1_out), .in_2(not_2_out), .Sum(half_adder_1_sum));  // open: Carry_Bit
  or or_1 (or_1_out, half_adder_3_carry_bit, half_adder_4_carry_bit);
  Half_Adder half_adder_2 (.in_1(half_adder_1_sum), .in_2(or_1_out), .Sum(out_9));  // open: Carry_Bit
  not not_3 (not_3_out, in_2);
  not not_4 (not_4_out, 1'b1);
  Half_Adder half_adder_3 (
    .Carry_Bit(half_adder_3_carry_bit), .in_1(not_3_out), .in_2(not_4_out), .Sum(half_adder_3_sum));
  Half_Adder half_adder_4 (.Carry_Bit(half_adder_4_carry_bit), .in_1(half_adder_3_sum), .in_2(or_2_out), .Sum(out_10));
  not not_5 (not_5_out, in_3);
  not not_6 (not_6_out, 1'b1);
  Half_Adder half_adder_5 (
    .Carry_Bit(half_adder_5_carry_bit), .in_1(not_5_out), .in_2(not_6_out), .Sum(half_adder_5_sum));
  or or_2 (or_2_out, half_adder_5_carry_bit, half_adder_6_carry_bit);
  Half_Adder half_adder_6 (.Carry_Bit(half_adder_6_carry_bit), .in_1(half_adder_5_sum), .in_2(or_3_out), .Sum(out_11));
  not not_7 (not_7_out, in_4);
  not not_8 (not_8_out, 1'b1);
  Half_Adder half_adder_7 (
    .Carry_Bit(half_adder_7_carry_bit), .in_1(not_7_out), .in_2(not_8_out), .Sum(half_adder_7_sum));
  or or_3 (or_3_out, half_adder_7_carry_bit, half_adder_8_carry_bit);
  Half_Adder half_adder_8 (.Carry_Bit(half_adder_8_carry_bit), .in_1(half_adder_7_sum), .in_2(or_4_out), .Sum(out_12));
  not not_9 (not_9_out, in_5);
  not not_10 (not_10_out, 1'b1);
  Half_Adder half_adder_9 (
    .Carry_Bit(half_adder_9_carry_bit), .in_1(not_9_out), .in_2(not_10_out), .Sum(half_adder_9_sum));
  or or_4 (or_4_out, half_adder_9_carry_bit, half_adder_10_carry_bit);
  Half_Adder half_adder_10 (
    .Carry_Bit(half_adder_10_carry_bit), .in_1(half_adder_9_sum), .in_2(or_5_out), .Sum(out_13));
  not not_11 (not_11_out, in_6);
  Half_Adder half_adder_11 (
    .Carry_Bit(half_adder_11_carry_bit), .in_1(not_11_out), .in_2(not_12_out), .Sum(half_adder_11_sum));
  or or_5 (or_5_out, half_adder_11_carry_bit, half_adder_12_carry_bit);
  Half_Adder half_adder_12 (
    .Carry_Bit(half_adder_12_carry_bit), .in_1(half_adder_11_sum), .in_2(or_6_out), .Sum(out_14));
  not not_12 (not_12_out, 1'b1);
  or or_6 (or_6_out, half_adder_13_carry_bit, half_adder_14_carry_bit);
  not not_13 (not_13_out, in_7);
  not not_14 (not_14_out, 1'b1);
  Half_Adder half_adder_13 (
    .Carry_Bit(half_adder_13_carry_bit), .in_1(not_13_out), .in_2(not_14_out), .Sum(half_adder_13_sum));
  Half_Adder half_adder_14 (
    .Carry_Bit(half_adder_14_carry_bit), .in_1(half_adder_13_sum), .in_2(half_adder_15_carry_bit),
    .Sum(out_15));
  not not_15 (not_15_out, in_8);
  Half_Adder half_adder_15 (.Carry_Bit(half_adder_15_carry_bit), .in_1(not_15_out), .in_2(1'b1), .Sum(out_16));

  // Notes on the sheet:
  //   2's Complement
endmodule
