// Logisim project 8-Bit Adder Output Analyser.circ as structural Verilog: 1 circuit, main circuit main
module main (
  input  in_1,
  input  in_2,
  input  in_3,
  input  in_4,
  input  in_5,
  input  in_6,
  input  in_7,
  input  in_8,
  input  in_9,
  output out_10,
  output out_11,
  output out_12,
  output out_13,
  output out_14,
  output out_15,
  output out_16,
  output out_17,
  output out_18,
  output out_19
);

  wire and_1_out, and_2_out, not_1_out, not_2_out, not_3_out, not_4_out, not_5_out, not_6_out, not_7_out,
       not_8_out;

  not not_1 (not_1_out, in_9);
  not not_2 (not_2_out, in_8);
  not not_3 (not_3_out, in_7);
  not not_4 (not_4_out, in_6);
  not not_5 (not_5_out, in_5);
  not not_6 (not_6_out, in_4);
  not not_7 (not_7_out, in_3);
  not not_8 (not_8_out, in_2);
  and and_1 (and_1_out, not_1_out, not_2_out, not_3_out, not_4_out);
  and and_2 (and_2_out, not_5_out, not_6_out, not_7_out, not_8_out);
  and and_3 (out_10, and_1_out, and_2_out);

  assign out_11 = in_1;
  assign out_12 = in_2;
  assign out_13 = in_3;
  assign out_14 = in_4;
  assign out_15 = in_5;
  assign out_16 = in_6;
  assign out_17 = in_7;
  assign out_18 = in_8;
  assign out_19 = in_9;

  // Notes on the sheet:
  //   Space for any other tests we want - we have 2 free bits/tests.
  //   1 if equal to 0
  //   1 if overflow
endmodule
