// Logisim project 8-Bit Adder.circ as structural Verilog: 1 circuit, main circuit main
module main (
  input  in_1,
  input  in_2,
  input  in_3,
  input  in_4,
  input  in_5,
  input  in_6,
  input  in_7,
  input  in_8,
  input  in_9,
  input  in_10,
  input  in_11,
  input  in_12,
  input  in_13,
  input  in_14,
  input  in_15,
  input  in_16,
  output Overflow,
  output out_18,
  output out_19,
  output out_20,
  output out_21,
  output out_22,
  output out_23,
  output out_24,
  output out_25
);

  wire half_adder_1_carry_bit, half_adder_1_sum, half_adder_2_carry_bit, half_adder_3_carry_bit,
       half_adder_3_sum, half_adder_4_carry_bit, half_adder_5_carry_bit, half_adder_5_sum,
       half_adder_6_carry_bit, half_adder_7_carry_bit, half_adder_7_sum, half_adder_8_carry_bit,
       half_adder_9_carry_bit, half_adder_9_sum, half_adder_10_carry_bit, half_adder_11_carry_bit,
       half_adder_11_sum, half_adder_12_carry_bit, half_adder_13_carry_bit, half_adder_13_sum,
       half_adder_14_carry_bit, half_adder_15_carry_bit, or_2_out, or_3_out, or_4_out, or_5_out, or_6_out,
       or_7_out;

  or or_1 (Overflow, half_adder_1_carry_bit, half_adder_2_carry_bit);
  Half_Adder half_adder_1 (.Carry_Bit(half_adder_1_carry_bit), .in_1(in_1), .in_2(in_9), .Sum(half_adder_1_sum));
  or or_2 (or_2_out, half_adder_3_carry_bit, half_adder_4_carry_bit);
  Half_Adder half_adder_2 (.Carry_Bit(half_adder_2_carry_bit), .in_1(half_adder_1_sum), .in_2(or_2_out), .Sum(out_18));
  Half_Adder half_adder_3 (.Carry_Bit(half_adder_3_carry_bit), .in_1(in_2), .in_2(in_10), .Sum(half_adder_3_sum));
  or or_3 (or_3_out, half_adder_5_carry_bit, half_adder_6_carry_bit);
  Half_Adder half_adder_4 (.Carry_Bit(half_adder_4_carry_bit), .in_1(half_adder_3_sum), .in_2(or_3_out), .Sum(out_19));
  Half_Adder half_adder_5 (.Carry_Bit(half_adder_5_carry_bit), .in_1(in_3), .in_2(in_11), .Sum(half_adder_5_sum));
  or or_4 (or_4_out, half_adder_7_carry_bit, half_adder_8_carry_bit);
  Half_Adder half_adder_6 (.Carry_Bit(half_adder_6_carry_bit), .in_1(half_adder_5_sum), .in_2(or_4_out), .Sum(out_20));
  Half_Adder half_adder_7 (.Carry_Bit(half_adder_7_carry_bit), .in_1(in_4), .in_2(in_12), .Sum(half_adder_7_sum));
  Half_Adder half_adder_8 (.Carry_Bit(half_adder_8_carry_bit), .in_1(half_adder_7_sum), .in_2(or_5_out), .Sum(out_21));
  Half_Adder half_adder_9 (.Carry_Bit(half_adder_9_carry_bit), .in_1(in_5), .in_2(in_13), .Sum(half_adder_9_sum));
  or or_5 (or_5_out, half_adder_9_carry_bit, half_adder_10_carry_bit);
  Half_Adder half_adder_10 (
    .Carry_Bit(half_adder_10_carry_bit), .in_1(half_adder_9_sum), .in_2(or_6_out), .Sum(out_22));
  Half_Adder half_adder_11 (.Carry_Bit(half_adder_11_carry_bit), .in_1(in_6), .in_2(in_14), .Sum(half_adder_11_sum));
  or or_6 (or_6_out, half_adder_11_carry_bit, half_adder_12_carry_bit);
  Half_Adder half_adder_12 (
    .Carry_Bit(half_adder_12_carry_bit), .in_1(half_adder_11_sum), .in_2(or_7_out), .Sum(out_23));
  Half_Adder half_adder_13 (.Carry_Bit(half_adder_13_carry_bit), .in_1(in_7), .in_2(in_15), .Sum(half_adder_13_sum));
  or or_7 (or_7_out, half_adder_13_carry_bit, half_adder_14_carry_bit);
  Half_Adder half_adder_14 (
    .Carry_Bit(half_adder_14_carry_bit), .in_1(half_adder_13_sum), .in_2(half_adder_15_carry_bit),
    .Sum(out_24));
  Half_Adder half_adder_15 (.Carry_Bit(half_adder_15_carry_bit), .in_1(in_8), .in_2(in_16), .Sum(out_25));

  // Notes on the sheet:
  //   Sum
endmodule
