// Logisim project ALU with multiplication.circ as structural Verilog: 3 circuits, main circuit main
module main (
  input  in_1,
  input  in_2,
  input  in_3,
  input  in_4,
  input  in_5,
  input  in_6,
  input  in_7,
  input  in_8,
  input  in_9,
  input  in_10,
  input  in_11,
  input  in_12,
  input  in_13,
  input  in_14,
  input  in_15,
  input  in_16,
  input  mult,
  input  sub,
  input  add,
  input  Clock,
  input  in_21,
  output Is_zero,
  output out_23,
  output out_24,
  output out_25,
  output out_26,
  output out_27,
  output out_28,
  output out_29,
  output out_30,
  output out_31,
  output out_32,
  output out_33
);

  wire alu_selector_1_out_19, alu_selector_1_out_20, alu_selector_1_out_21, alu_selector_1_out_22,
       alu_selector_1_out_23, alu_selector_1_out_24, alu_selector_1_out_25, alu_selector_1_out_26, and_1_out,
       and_2_out, and_11_out, and_12_out, main_1_out_10, main_1_out_11, main_1_out_12, main_1_out_13,
       main_1_out_14, main_1_out_15, main_1_out_16, main_1_out_17, main_2_out_9, main_2_out_10,
       main_2_out_11, main_2_out_12, main_2_out_13, main_2_out_14, main_2_out_15, main_2_out_16,
       main_3_out_18, main_3_out_19, main_3_out_20, main_3_out_21, main_3_out_22, main_3_out_23,
       main_3_out_24, main_3_out_25, main_3_overflow, main_4_out_10, main_4_out_11, main_4_out_12,
       main_4_out_13, main_4_out_14, main_4_out_15, main_4_out_16, main_4_out_17, main_4_out_18,
       main_4_out_19, main_5_out_10, main_5_out_11, main_5_out_12, main_5_out_13, main_5_out_14,
       main_5_out_15, main_5_out_16, main_5_out_17, main_6_out_19, main_6_out_20, main_6_out_21,
       main_6_out_22, main_6_out_23, main_6_out_24, main_6_out_25, main_6_out_26, main_6_out_27,
       main_7_out_7, not_1_out, not_2_out, not_3_out, or_1_out, or_2_out, or_3_out, or_4_out, or_5_out,
       or_6_out, or_7_out, or_8_out, or_9_out, output_register_1_out_11, output_register_1_out_12,
       output_register_1_out_13, output_register_1_out_14, output_register_1_out_15,
       output_register_1_out_16, output_register_1_out_17, output_register_1_out_18;

  not not_1 (not_1_out, mult);
  or or_1 (or_1_out, sub, add);
  and and_1 (and_1_out, mult, Clock);
  and and_2 (and_2_out, not_1_out, or_1_out, Clock);
  or or_2 (or_2_out, output_register_1_out_11, main_6_out_19);
  buf and_3 (out_26, or_2_out);  // AND_Gate
  ALU_selector alu_selector_1 (
    ._2_s_complement(sub), .in_18(add), .in_1(main_1_out_10), .in_2(main_1_out_11), .in_3(main_1_out_12),
    .in_4(main_1_out_13), .in_5(main_1_out_14), .in_6(main_1_out_15), .in_7(main_1_out_16),
    .in_8(main_1_out_17), .in_9(main_2_out_9), .in_10(main_2_out_10), .in_11(main_2_out_11),
    .in_12(main_2_out_12), .in_13(main_2_out_13), .in_14(main_2_out_14), .in_15(main_2_out_15),
    .in_16(main_2_out_16), .out_19(alu_selector_1_out_19), .out_20(alu_selector_1_out_20),
    .out_21(alu_selector_1_out_21), .out_22(alu_selector_1_out_22), .out_23(alu_selector_1_out_23),
    .out_24(alu_selector_1_out_24), .out_25(alu_selector_1_out_25), .out_26(alu_selector_1_out_26));
  or or_3 (or_3_out, output_register_1_out_12, main_6_out_20);
  buf and_4 (out_27, or_3_out);  // AND_Gate
  _8_Bit_Register_main main_1 (
    .Clock(and_2_out), .in_1(in_1), .in_2(in_2), .in_3(in_3), .in_4(in_4), .in_5(in_5), .in_6(in_6),
    .in_7(in_7), .in_8(in_8), .out_10(main_1_out_10), .out_11(main_1_out_11), .out_12(main_1_out_12),
    .out_13(main_1_out_13), .out_14(main_1_out_14), .out_15(main_1_out_15), .out_16(main_1_out_16),
    .out_17(main_1_out_17));
  _8_Bit_2_s_Complement_main main_2 (
    .in_1(main_1_out_10), .in_2(main_1_out_11), .in_3(main_1_out_12), .in_4(main_1_out_13),
    .in_5(main_1_out_14), .in_6(main_1_out_15), .in_7(main_1_out_16), .in_8(main_1_out_17),
    .out_9(main_2_out_9), .out_10(main_2_out_10), .out_11(main_2_out_11), .out_12(main_2_out_12),
    .out_13(main_2_out_13), .out_14(main_2_out_14), .out_15(main_2_out_15), .out_16(main_2_out_16));
  or or_4 (or_4_out, output_register_1_out_13, main_6_out_21);
  buf and_5 (out_28, or_4_out);  // AND_Gate
  _8_Bit_Adder_main main_3 (
    .in_1(alu_selector_1_out_19), .in_2(alu_selector_1_out_20), .in_3(alu_selector_1_out_21),
    .in_4(alu_selector_1_out_22), .in_5(alu_selector_1_out_23), .in_6(alu_selector_1_out_24),
    .in_7(alu_selector_1_out_25), .in_8(alu_selector_1_out_26), .in_9(main_5_out_10), .in_10(main_5_out_11),
    .in_11(main_5_out_12), .in_12(main_5_out_13), .in_13(main_5_out_14), .in_14(main_5_out_15),
    .in_15(main_5_out_16), .in_16(main_5_out_17), .Overflow(main_3_overflow), .out_18(main_3_out_18),
    .out_19(main_3_out_19), .out_20(main_3_out_20), .out_21(main_3_out_21), .out_22(main_3_out_22),
    .out_23(main_3_out_23), .out_24(main_3_out_24), .out_25(main_3_out_25));
  buf and_6 (out_29, or_5_out);  // AND_Gate
  output_register output_register_1 (
    .Clock(and_2_out), .in_10(in_21), .in_1(main_4_out_12), .in_2(main_4_out_13), .in_3(main_4_out_14),
    .in_4(main_4_out_15), .in_5(main_4_out_16), .in_6(main_4_out_17), .in_7(main_4_out_18),
    .in_8(main_4_out_19), .out_11(output_register_1_out_11), .out_12(output_register_1_out_12),
    .out_13(output_register_1_out_13), .out_14(output_register_1_out_14), .out_15(output_register_1_out_15),
    .out_16(output_register_1_out_16), .out_17(output_register_1_out_17), .out_18(output_register_1_out_18));
  or or_5 (or_5_out, output_register_1_out_14, main_6_out_22);
  _8_Bit_Adder_Output_Analyser_main main_4 (
    .out_10(main_4_out_10), .out_11(main_4_out_11), .in_1(main_3_overflow), .in_2(main_3_out_18),
    .in_3(main_3_out_19), .in_4(main_3_out_20), .in_5(main_3_out_21), .in_6(main_3_out_22),
    .in_7(main_3_out_23), .in_8(main_3_out_24), .in_9(main_3_out_25), .out_12(main_4_out_12),
    .out_13(main_4_out_13), .out_14(main_4_out_14), .out_15(main_4_out_15), .out_16(main_4_out_16),
    .out_17(main_4_out_17), .out_18(main_4_out_18), .out_19(main_4_out_19));
  or or_6 (or_6_out, output_register_1_out_15, main_6_out_23);
  buf and_7 (out_30, or_6_out);  // AND_Gate
  _8_Bit_Register_main main_5 (
    .Clock(and_2_out), .in_1(in_9), .in_2(in_10), .in_3(in_11), .in_4(in_12), .in_5(in_13), .in_6(in_14),
    .in_7(in_15), .in_8(in_16), .out_10(main_5_out_10), .out_11(main_5_out_11), .out_12(main_5_out_12),
    .out_13(main_5_out_13), .out_14(main_5_out_14), .out_15(main_5_out_15), .out_16(main_5_out_16),
    .out_17(main_5_out_17));
  or or_7 (or_7_out, output_register_1_out_16, main_6_out_24);
  buf and_8 (out_31, or_7_out);  // AND_Gate
  or or_8 (or_8_out, output_register_1_out_17, main_6_out_25);
  buf and_9 (out_32, or_8_out);  // AND_Gate
  or or_9 (or_9_out, output_register_1_out_18, main_6_out_26);
  buf and_10 (out_33, or_9_out);  // AND_Gate
  Multiplier_main main_6 (
    .in_17(and_1_out), .in_1(in_1), .in_2(in_2), .in_3(in_3), .in_4(in_4), .in_5(in_5), .in_6(in_6),
    .in_7(in_7), .in_8(in_8), .in_9(in_9), .in_10(in_10), .in_11(in_11), .in_12(in_12), .in_13(in_13),
    .in_14(in_14), .in_15(in_15), .in_16(in_16), .out_19(main_6_out_19), .out_20(main_6_out_20),
    .out_21(main_6_out_21), .out_22(main_6_out_22), .out_23(main_6_out_23), .out_24(main_6_out_24),
    .out_25(main_6_out_25), .out_26(main_6_out_26), .out_27(main_6_out_27), .in_18(not_2_out));
  not not_2 (not_2_out, sub);
  _4_Bit_Register_main main_7 (
    .Clock(and_2_out), .in_1(main_4_out_10), .in_2(main_4_out_11), .out_6(Is_zero), .out_7(main_7_out_7),
    .out_8(out_24), .out_9(out_25));  // open: in_3, in_4
  not not_3 (not_3_out, sub);
  and and_11 (and_11_out, main_7_out_7, not_3_out);
  and and_12 (and_12_out, main_6_out_27, and_1_out);
  or or_10 (out_23, and_11_out, and_12_out);

  // Notes on the sheet:
  //   reset
  //   unable add & sub
  //   Adder
  //   Output Analyser
  //   Input Registers
  //   Output Register
  //   overflow
  //   Status Register
  //   Overflow?
endmodule

module ALU_selector (
  input  in_1,
  input  in_2,
  input  in_3,
  input  in_4,
  input  in_5,
  input  in_6,
  input  in_7,
  input  in_8,
  input  in_9,
  input  in_10,
  input  in_11,
  input  in_12,
  input  in_13,
  input  in_14,
  input  in_15,
  input  in_16,
  input  _2_s_complement,
  input  in_18,
  output out_19,
  output out_20,
  output out_21,
  output out_22,
  output out_23,
  output out_24,
  output out_25,
  output out_26
);

  wire and_1_out, and_2_out, and_3_out, and_4_out, and_5_out, and_6_out, and_7_out, and_8_out, and_9_out,
       and_10_out, and_11_out, and_12_out, and_13_out, and_14_out, and_15_out, and_16_out;

  and and_1 (and_1_out, in_18, in_1);
  or or_1 (out_19, and_1_out, and_2_out);
  and and_2 (and_2_out, _2_s_complement, in_9);
  and and_3 (and_3_out, in_18, in_2);
  and and_4 (and_4_out, _2_s_complement, in_10);
  or or_2 (out_20, and_3_out, and_4_out);
  and and_5 (and_5_out, in_18, in_3);
  and and_6 (and_6_out, _2_s_complement, in_11);
  or or_3 (out_21, and_5_out, and_6_out);
  and and_7 (and_7_out, in_18, in_4);
  and and_8 (and_8_out, _2_s_complement, in_12);
  or or_4 (out_22, and_7_out, and_8_out);
  and and_9 (and_9_out, in_18, in_5);
  or or_5 (out_23, and_9_out, and_10_out);
  and and_10 (and_10_out, _2_s_complement, in_13);
  and and_11 (and_11_out, in_18, in_6);
  or or_6 (out_24, and_11_out, and_12_out);
  and and_12 (and_12_out, _2_s_complement, in_14);
  and and_13 (and_13_out, in_18, in_7);
  and and_14 (and_14_out, _2_s_complement, in_15);
  or or_7 (out_25, and_13_out, and_14_out);
  and and_15 (and_15_out, in_18, in_8);
  and and_16 (and_16_out, _2_s_complement, in_16);
  or or_8 (out_26, and_15_out, and_16_out);

  // Notes on the sheet:
  //   2's complement
endmodule

module output_register (
  input  in_1,
  input  in_2,
  input  in_3,
  input  in_4,
  input  in_5,
  input  in_6,
  input  in_7,
  input  in_8,
  input  Clock,
  input  in_10,
  output out_11,
  output out_12,
  output out_13,
  output out_14,
  output out_15,
  output out_16,
  output out_17,
  output out_18
);

  D_Flip_Flop d_ff_1 (.clk(Clock), .D(in_1), .Q(out_11), .reset(in_10));  // open: Qn, preset, en
  D_Flip_Flop d_ff_2 (.clk(Clock), .D(in_2), .Q(out_12), .reset(in_10));  // open: Qn, preset, en
  D_Flip_Flop d_ff_3 (.clk(Clock), .D(in_3), .Q(out_13), .reset(in_10));  // open: Qn, preset, en
  D_Flip_Flop d_ff_4 (.clk(Clock), .D(in_4), .Q(out_14), .reset(in_10));  // open: Qn, preset, en
  D_Flip_Flop d_ff_5 (.clk(Clock), .D(in_5), .Q(out_15), .reset(in_10));  // open: Qn, preset, en
  D_Flip_Flop d_ff_6 (.clk(Clock), .D(in_6), .Q(out_16), .reset(in_10));  // open: Qn, preset, en
  D_Flip_Flop d_ff_7 (.clk(Clock), .D(in_7), .Q(out_17), .reset(in_10));  // open: Qn, preset, en
  D_Flip_Flop d_ff_8 (.clk(Clock), .D(in_8), .Q(out_18), .reset(in_10));  // open: Qn, preset, en
endmodule
