// Logisim project Data Cache.circ as structural Verilog: 7 circuits, main circuit BYTE
module BYTE (
  input  in_1,
  input  in_2,
  input  in_3,
  input  Clock,
  input  [7:0] in_5,
  input  in_6,
  output out_7,
  output out_8,
  output out_9,
  output out_10,
  output out_11,
  output out_12,
  output out_13,
  output out_14
);

  wire and_1_out, and_2_out, d_ff_1_q, d_ff_2_q, d_ff_3_q, d_ff_4_q, d_ff_5_q, d_ff_6_q, d_ff_7_q, d_ff_8_q;

  and and_1 (and_1_out, in_2, in_3);
  and and_2 (and_2_out, and_1_out, Clock);
  D_Flip_Flop d_ff_1 (.clk(and_2_out), .D(in_5[0]), .Q(d_ff_1_q), .reset(in_6));  // open: Qn, preset, en
  D_Flip_Flop d_ff_2 (.clk(and_2_out), .D(in_5[1]), .Q(d_ff_2_q), .reset(in_6));  // open: Qn, preset, en
  D_Flip_Flop d_ff_3 (.clk(and_2_out), .D(in_5[2]), .Q(d_ff_3_q), .reset(in_6));  // open: Qn, preset, en
  D_Flip_Flop d_ff_4 (.clk(and_2_out), .D(in_5[3]), .Q(d_ff_4_q), .reset(in_6));  // open: Qn, preset, en
  D_Flip_Flop d_ff_5 (.clk(and_2_out), .D(in_5[4]), .Q(d_ff_5_q), .reset(in_6));  // open: Qn, preset, en
  D_Flip_Flop d_ff_6 (.clk(and_2_out), .D(in_5[5]), .Q(d_ff_6_q), .reset(in_6));  // open: Qn, preset, en
  D_Flip_Flop d_ff_7 (.clk(and_2_out), .D(in_5[6]), .Q(d_ff_7_q), .reset(in_6));  // open: Qn, preset, en
  D_Flip_Flop d_ff_8 (.clk(and_2_out), .D(in_5[7]), .Q(d_ff_8_q), .reset(in_6));  // open: Qn, preset, en
  and and_3 (out_7, in_1, d_ff_1_q);
  and and_4 (out_8, in_1, d_ff_2_q);
  and and_5 (out_9, in_1, d_ff_3_q);
  and and_6 (out_10, in_1, d_ff_4_q);
  and and_7 (out_11, in_1, d_ff_5_q);
  and and_8 (out_12, in_1, d_ff_6_q);
  and and_9 (out_13, in_1, d_ff_7_q);
  and and_10 (out_14, in_1, d_ff_8_q);
endmodule

module main (
  input  in_1,
  input  address,
  input  in_3,
  input  in_4,
  input  read,
  input  write,
  input  in_7,
  input  in_8,
  input  in_9,
  input  data,
  input  in_11,
  input  in_12,
  input  in_13,
  input  in_14,
  input  Clock,
  input  Zero,
  output out_17,
  output out_18,
  output out_19,
  output out_20,
  output out_21,
  output out_22,
  output out_23,
  output out_24
);

  wire address_director_1_out_2, address_director_1_out_3, address_director_1_out_4,
       address_director_1_out_5, address_director_1_out_6, address_director_1_out_7,
       address_director_1_out_8, address_director_1_out_9, address_director_1_out_10,
       address_director_1_out_11, address_director_1_out_12, address_director_1_out_13,
       address_director_1_out_14, address_director_1_out_15, address_director_1_out_16,
       address_director_1_out_17;
  wire [7:0] n4_bytes_1_out_10, n4_bytes_1_out_11, n4_bytes_1_out_12, n4_bytes_1_out_13, n4_bytes_2_out_10,
       n4_bytes_2_out_11, n4_bytes_2_out_12, n4_bytes_2_out_13, n4_bytes_3_out_10, n4_bytes_3_out_11,
       n4_bytes_3_out_12, n4_bytes_3_out_13, n4_bytes_4_out_10, n4_bytes_4_out_11, n4_bytes_4_out_12,
       n4_bytes_4_out_13;

  Address_Director address_director_1 (
    .in_1({in_4, in_3, address, in_1}), .out_2(address_director_1_out_2), .out_3(address_director_1_out_3),
    .out_4(address_director_1_out_4), .out_5(address_director_1_out_5), .out_6(address_director_1_out_6),
    .out_7(address_director_1_out_7), .out_8(address_director_1_out_8), .out_9(address_director_1_out_9),
    .out_10(address_director_1_out_10), .out_11(address_director_1_out_11),
    .out_12(address_director_1_out_12), .out_13(address_director_1_out_13),
    .out_14(address_director_1_out_14), .out_15(address_director_1_out_15),
    .out_16(address_director_1_out_16), .out_17(address_director_1_out_17));
  _4_bytes u_4_bytes_1 (
    .W(write), .AddCheck1(address_director_1_out_2), .AddCheck2(address_director_1_out_3),
    .AddCheck3(address_director_1_out_4), .AddCheck4(address_director_1_out_5),
    .in_6({in_14, in_13, in_12, in_11, data, in_9, in_8, in_7}), .R(read), .Clock(Clock), .Zero(Zero),
    .out_10(n4_bytes_1_out_10), .out_11(n4_bytes_1_out_11), .out_12(n4_bytes_1_out_12),
    .out_13(n4_bytes_1_out_13));
  _4_bytes u_4_bytes_2 (
    .W(write), .AddCheck1(address_director_1_out_6), .AddCheck2(address_director_1_out_7),
    .AddCheck3(address_director_1_out_8), .AddCheck4(address_director_1_out_9),
    .in_6({in_14, in_13, in_12, in_11, data, in_9, in_8, in_7}), .R(read), .Clock(Clock), .Zero(Zero),
    .out_10(n4_bytes_2_out_10), .out_11(n4_bytes_2_out_11), .out_12(n4_bytes_2_out_12),
    .out_13(n4_bytes_2_out_13));
  _4_bytes u_4_bytes_3 (
    .W(write), .AddCheck1(address_director_1_out_10), .AddCheck2(address_director_1_out_11),
    .AddCheck3(address_director_1_out_12), .AddCheck4(address_director_1_out_13),
    .in_6({in_14, in_13, in_12, in_11, data, in_9, in_8, in_7}), .R(read), .Clock(Clock), .Zero(Zero),
    .out_10(n4_bytes_3_out_10), .out_11(n4_bytes_3_out_11), .out_12(n4_bytes_3_out_12),
    .out_13(n4_bytes_3_out_13));
  _4_bytes u_4_bytes_4 (
    .W(write), .AddCheck1(address_director_1_out_14), .AddCheck2(address_director_1_out_15),
    .AddCheck3(address_director_1_out_16), .AddCheck4(address_director_1_out_17),
    .in_6({in_14, in_13, in_12, in_11, data, in_9, in_8, in_7}), .R(read), .Clock(Clock), .Zero(Zero),
    .out_10(n4_bytes_4_out_10), .out_11(n4_bytes_4_out_11), .out_12(n4_bytes_4_out_12),
    .out_13(n4_bytes_4_out_13));
  assign {out_17, out_18, out_19, out_20, out_21, out_22, out_23, out_24} = n4_bytes_1_out_10 | n4_bytes_1_out_11 | n4_bytes_1_out_12 | n4_bytes_1_out_13 | n4_bytes_2_out_10 | n4_bytes_2_out_11 | n4_bytes_2_out_12 | n4_bytes_2_out_13 | n4_bytes_3_out_10 | n4_bytes_3_out_11 | n4_bytes_3_out_12 | n4_bytes_3_out_13 | n4_bytes_4_out_10 | n4_bytes_4_out_11 | n4_bytes_4_out_12 | n4_bytes_4_out_13;  // OR_Gate or_1, 8 bits wide
endmodule

module ADD_Check (
  input  in_1,
  input  in_2,
  input  in_3,
  output out_4,
  output out_5,
  output out_6,
  output out_7
);

  wire and_1_out, and_2_out, and_3_out, not_1_out, not_2_out, not_3_out, not_4_out;

  and and_1 (and_1_out, in_1, in_3);
  and and_2 (and_2_out, in_2, in_3);
  not not_1 (not_1_out, and_1_out);
  not not_2 (not_2_out, and_2_out);
  not not_3 (not_3_out, and_2_out);
  not not_4 (not_4_out, and_1_out);
  and and_3 (and_3_out, not_1_out, not_2_out);
  and and_4 (out_5, and_1_out, not_3_out);
  and and_5 (out_6, not_4_out, and_2_out);
  and and_6 (out_7, and_1_out, and_2_out);
  and and_7 (out_4, in_3, and_3_out);
endmodule

module Address_Director (
  input  [3:0] in_1,
  output out_2,
  output out_3,
  output out_4,
  output out_5,
  output out_6,
  output out_7,
  output out_8,
  output out_9,
  output out_10,
  output out_11,
  output out_12,
  output out_13,
  output out_14,
  output out_15,
  output out_16,
  output out_17
);

  wire add_check_1_out_4, add_check_1_out_5, add_check_1_out_6, add_check_1_out_7;

  ADD_Check add_check_1 (
    .in_1(in_1[2]), .in_2(in_1[3]), .in_3(1'b1), .out_4(add_check_1_out_4), .out_5(add_check_1_out_5),
    .out_6(add_check_1_out_6), .out_7(add_check_1_out_7));
  ADD_Check add_check_2 (
    .in_1(in_1[0]), .in_2(in_1[1]), .in_3(add_check_1_out_4), .out_4(out_2), .out_5(out_3), .out_6(out_4),
    .out_7(out_5));
  ADD_Check add_check_3 (
    .in_1(in_1[0]), .in_2(in_1[1]), .in_3(add_check_1_out_5), .out_4(out_6), .out_5(out_7), .out_6(out_8),
    .out_7(out_9));
  ADD_Check add_check_4 (
    .in_1(in_1[0]), .in_2(in_1[1]), .in_3(add_check_1_out_6), .out_4(out_10), .out_5(out_11), .out_6(out_12),
    .out_7(out_13));
  ADD_Check add_check_5 (
    .in_1(in_1[0]), .in_2(in_1[1]), .in_3(add_check_1_out_7), .out_4(out_14), .out_5(out_15), .out_6(out_16),
    .out_7(out_17));
endmodule

module _1_bit_to_8_bit (
  input  in_1,
  output [7:0] out_2
);


  assign out_2 = {8{in_1}};
endmodule

module _4_bytes (
  input  W,
  input  AddCheck1,
  input  AddCheck2,
  input  AddCheck3,
  input  AddCheck4,
  input  [7:0] in_6,
  input  R,
  input  Clock,
  input  Zero,
  output [7:0] out_10,
  output [7:0] out_11,
  output [7:0] out_12,
  output [7:0] out_13
);

  wire [7:0] byte_1_out_14, byte_2_out_14, byte_3_out_14, byte_4_out_14, n1_bit_to_8_bit_1_out_2,
       n1_bit_to_8_bit_2_out_2, n1_bit_to_8_bit_3_out_2, n1_bit_to_8_bit_4_out_2;

  BYTE byte_1 (
    .in_1(R), .in_2(W), .in_3(AddCheck1), .Clock(Clock), .in_5(in_6), .in_6(Zero), .out_7(byte_1_out_14[7]),
    .out_8(byte_1_out_14[6]), .out_9(byte_1_out_14[5]), .out_10(byte_1_out_14[4]), .out_11(byte_1_out_14[3]),
    .out_12(byte_1_out_14[2]), .out_13(byte_1_out_14[1]), .out_14(byte_1_out_14[0]));
  BYTE byte_2 (
    .in_1(R), .in_2(W), .in_3(AddCheck2), .Clock(Clock), .in_5(in_6), .in_6(Zero), .out_7(byte_2_out_14[7]),
    .out_8(byte_2_out_14[6]), .out_9(byte_2_out_14[5]), .out_10(byte_2_out_14[4]), .out_11(byte_2_out_14[3]),
    .out_12(byte_2_out_14[2]), .out_13(byte_2_out_14[1]), .out_14(byte_2_out_14[0]));
  BYTE byte_3 (
    .in_1(R), .in_2(W), .in_3(AddCheck3), .Clock(Clock), .in_5(in_6), .in_6(Zero), .out_7(byte_3_out_14[7]),
    .out_8(byte_3_out_14[6]), .out_9(byte_3_out_14[5]), .out_10(byte_3_out_14[4]), .out_11(byte_3_out_14[3]),
    .out_12(byte_3_out_14[2]), .out_13(byte_3_out_14[1]), .out_14(byte_3_out_14[0]));
  BYTE byte_4 (
    .in_1(R), .in_2(W), .in_3(AddCheck4), .Clock(Clock), .in_5(in_6), .in_6(Zero), .out_7(byte_4_out_14[7]),
    .out_8(byte_4_out_14[6]), .out_9(byte_4_out_14[5]), .out_10(byte_4_out_14[4]), .out_11(byte_4_out_14[3]),
    .out_12(byte_4_out_14[2]), .out_13(byte_4_out_14[1]), .out_14(byte_4_out_14[0]));
  _1_bit_to_8_bit u_1_bit_to_8_bit_1 (.in_1(AddCheck1), .out_2(n1_bit_to_8_bit_1_out_2));
  _1_bit_to_8_bit u_1_bit_to_8_bit_2 (.in_1(AddCheck2), .out_2(n1_bit_to_8_bit_2_out_2));
  _1_bit_to_8_bit u_1_bit_to_8_bit_3 (.in_1(AddCheck3), .out_2(n1_bit_to_8_bit_3_out_2));
  _1_bit_to_8_bit u_1_bit_to_8_bit_4 (.in_1(AddCheck4), .out_2(n1_bit_to_8_bit_4_out_2));
  assign out_10 = byte_1_out_14 & n1_bit_to_8_bit_1_out_2;  // AND_Gate and_1, 8 bits wide
  assign out_11 = byte_2_out_14 & n1_bit_to_8_bit_2_out_2;  // AND_Gate and_2, 8 bits wide
  assign out_12 = byte_3_out_14 & n1_bit_to_8_bit_3_out_2;  // AND_Gate and_3, 8 bits wide
  assign out_13 = byte_4_out_14 & n1_bit_to_8_bit_4_out_2;  // AND_Gate and_4, 8 bits wide
endmodule

module main_4bytes (
  input  in_1,
  input  address,
  input  in_3,
  input  in_4,
  input  read,
  input  write,
  input  in_7,
  input  in_8,
  input  in_9,
  input  data,
  input  in_11,
  input  in_12,
  input  in_13,
  input  in_14,
  input  Clock,
  input  Zero,
  output out_17,
  output out_18,
  output out_19,
  output out_20,
  output out_21,
  output out_22,
  output out_23,
  output out_24
);

  wire and_1_out, and_2_out, and_3_out, and_4_out, not_1_out, not_2_out, not_3_out, not_4_out, not_5_out,
       not_6_out, not_7_out, not_8_out, not_9_out, not_10_out;
  wire [7:0] byte_1_out_7, byte_2_out_7, byte_3_out_7, byte_4_out_7;

  not not_1 (not_1_out, in_1);
  not not_2 (not_2_out, address);
  not not_3 (not_3_out, in_3);
  not not_4 (not_4_out, in_4);
  not not_5 (not_5_out, in_1);
  not not_6 (not_6_out, address);
  not not_7 (not_7_out, in_4);
  not not_8 (not_8_out, in_1);
  not not_9 (not_9_out, address);
  not not_10 (not_10_out, in_3);
  and and_1 (and_1_out, not_1_out, not_2_out, not_4_out, not_3_out);
  and and_2 (and_2_out, not_5_out, not_6_out, not_7_out, in_3);
  and and_3 (and_3_out, not_8_out, not_9_out, in_4, not_10_out);
  and and_4 (and_4_out, in_1, address, in_4, in_3);
  BYTE byte_1 (
    .in_1(read), .in_2(write), .in_3(and_1_out), .Clock(Clock),
    .in_5({in_14, in_13, in_12, in_11, data, in_9, in_8, in_7}), .in_6(Zero), .out_7(byte_1_out_7[0]),
    .out_8(byte_1_out_7[1]), .out_9(byte_1_out_7[2]), .out_10(byte_1_out_7[3]), .out_11(byte_1_out_7[4]),
    .out_12(byte_1_out_7[5]), .out_13(byte_1_out_7[6]), .out_14(byte_1_out_7[7]));
  BYTE byte_2 (
    .in_1(read), .in_2(write), .in_3(Clock), .Clock(and_2_out),
    .in_5({in_14, in_13, in_12, in_11, data, in_9, in_8, in_7}), .in_6(Zero), .out_7(byte_2_out_7[0]),
    .out_8(byte_2_out_7[1]), .out_9(byte_2_out_7[2]), .out_10(byte_2_out_7[3]), .out_11(byte_2_out_7[4]),
    .out_12(byte_2_out_7[5]), .out_13(byte_2_out_7[6]), .out_14(byte_2_out_7[7]));
  BYTE byte_3 (
    .in_1(read), .in_2(write), .in_3(Clock), .Clock(and_3_out),
    .in_5({in_14, in_13, in_12, in_11, data, in_9, in_8, in_7}), .in_6(Zero), .out_7(byte_3_out_7[0]),
    .out_8(byte_3_out_7[1]), .out_9(byte_3_out_7[2]), .out_10(byte_3_out_7[3]), .out_11(byte_3_out_7[4]),
    .out_12(byte_3_out_7[5]), .out_13(byte_3_out_7[6]), .out_14(byte_3_out_7[7]));
  BYTE byte_4 (
    .in_1(read), .in_2(write), .in_3(Clock), .Clock(and_4_out),
    .in_5({in_14, in_13, in_12, in_11, data, in_9, in_8, in_7}), .in_6(Zero), .out_7(byte_4_out_7[0]),
    .out_8(byte_4_out_7[1]), .out_9(byte_4_out_7[2]), .out_10(byte_4_out_7[3]), .out_11(byte_4_out_7[4]),
    .out_12(byte_4_out_7[5]), .out_13(byte_4_out_7[6]), .out_14(byte_4_out_7[7]));
  assign {out_17, out_18, out_19, out_20, out_21, out_22, out_23, out_24} = byte_1_out_7 | byte_2_out_7 | byte_3_out_7 | byte_4_out_7;  // OR_Gate or_1, 8 bits wide
endmodule
