// Logisim project Flip-Flop (Clocked RS).circ as structural Verilog: 1 circuit, main circuit main
module main (
  input  in_1,
  input  Clock,
  output out_3,
  output out_4
);

  wire and_1_out, and_2_out, not_1_out, or_1_out, or_2_out;

  not not_1 (not_1_out, in_1);
  and and_1 (and_1_out, in_1, Clock);
  and and_2 (and_2_out, Clock, not_1_out);
  or or_1 (or_1_out, out_4, and_1_out);
  not not_2 (out_3, or_1_out);
  or or_2 (or_2_out, and_2_out, out_3);
  not not_3 (out_4, or_2_out);
endmodule
