// Logisim project General Purpose Register.circ as structural Verilog: 1 circuit, main circuit main
module main (
  input  in_1,
  input  in_2,
  input  in_3,
  input  in_4,
  input  in_5,
  input  in_6,
  input  in_7,
  input  in_8,
  input  in_9,
  input  clock,
  input  load,
  input  in_12,
  input  ALU,
  input  read,
  input  On_Off,
  output out_16,
  output out_17,
  output out_18,
  output out_19,
  output out_20,
  output out_21,
  output out_22,
  output out_23
);

  wire and_1_out, and_2_out, or_1_out, or_2_out;

  or or_1 (or_1_out, in_7, in_12);
  and and_1 (and_1_out, or_1_out, or_2_out);
  and and_2 (and_2_out, clock, and_1_out);
  D_Flip_Flop d_ff_1 (.clk(and_2_out), .D(in_8), .Q(out_22), .reset(On_Off));  // open: Qn, preset, en
  D_Flip_Flop d_ff_2 (.clk(and_2_out), .D(in_9), .Q(out_23), .reset(On_Off));  // open: Qn, preset, en
  D_Flip_Flop d_ff_3 (.clk(and_2_out), .D(in_1), .Q(out_16), .reset(On_Off));  // open: Qn, preset, en
  D_Flip_Flop d_ff_4 (.clk(and_2_out), .D(in_2), .Q(out_17), .reset(On_Off));  // open: Qn, preset, en
  D_Flip_Flop d_ff_5 (.clk(and_2_out), .D(in_3), .Q(out_18), .reset(On_Off));  // open: Qn, preset, en
  D_Flip_Flop d_ff_6 (.clk(and_2_out), .D(in_4), .Q(out_19), .reset(On_Off));  // open: Qn, preset, en
  D_Flip_Flop d_ff_7 (.clk(and_2_out), .D(in_5), .Q(out_20), .reset(On_Off));  // open: Qn, preset, en
  D_Flip_Flop d_ff_8 (.clk(and_2_out), .D(in_6), .Q(out_21), .reset(On_Off));  // open: Qn, preset, en
  or or_2 (or_2_out, load, ALU, read);
endmodule
