// Logisim project Half Adder.circ as structural Verilog: 1 circuit, main circuit Half Adder
module Half_Adder (
  input  in_1,
  input  in_2,
  output Carry_Bit,
  output Sum
);

  wire not_1_out, or_1_out;

  and and_1 (Carry_Bit, in_1, in_2);
  not not_1 (not_1_out, Carry_Bit);
  or or_1 (or_1_out, in_1, in_2);
  and and_2 (Sum, not_1_out, or_1_out);
endmodule
