// Logisim project Input Reader.circ as structural Verilog: 1 circuit, main circuit main
module main (
  input  _1,
  input  _2,
  input  _3,
  input  _4,
  input  _5,
  input  _6,
  input  _7,
  input  _8,
  input  _9,
  input  _0,
  output out_11,
  output out_12,
  output out_13,
  output out_14,
  output out_15,
  output out_16,
  output out_17,
  output out_18
);

  not not_1 (out_15, 1'b1);
  not not_2 (out_17, 1'b1);
  not not_3 (out_16, 1'b1);
  not not_4 (out_18, 1'b1);
  or or_1 (out_11, _8, _9);
  or or_2 (out_12, _4, _5, _6, _7);
  or or_3 (out_13, _2, _3, _6, _7);
  or or_4 (out_14, _1, _3, _5, _7, _9);
endmodule
