// Logisim project Program Counter.circ as structural Verilog: 7 circuits, main circuit main
module main (
  input  in_1,
  input  in_2,
  input  in_3,
  input  in_4,
  input  clock,
  input  stop,
  input  bz_bnz,
  input  on_off,
  output out_9,
  output out_10,
  output out_11,
  output out_12
);

  wire and_1_out, bz_1_out_10, bz_1_out_11, bz_1_out_12, bz_1_out_13, counter_1_out_3, counter_1_out_4,
       counter_1_out_5, counter_1_out_6, main_1_out_22, main_1_out_23, main_1_out_24, main_1_out_25,
       n4tick_1tick_1_out_3, not_1_out, not_2_out, or_1_out, register_immediate_output_1_out_6,
       register_immediate_output_1_out_7, register_immediate_output_1_out_8,
       register_immediate_output_1_out_9, register_immediate_output_2_out_6,
       register_immediate_output_2_out_7, register_immediate_output_2_out_8,
       register_immediate_output_2_out_9, undriven, undriven_2, undriven_3;

  not not_1 (not_1_out, stop);
  and and_1 (and_1_out, clock, not_1_out);
  not not_2 (not_2_out, on_off);
  or or_1 (or_1_out, bz_bnz, on_off);
  _4tick_1tick u_4tick_1tick_1 (.in_1(and_1_out), .out_3(n4tick_1tick_1_out_3));  // open: in_2
  and and_2 (out_9, not_2_out, register_immediate_output_2_out_6);
  register_immediate_output register_immediate_output_1 (
    .in_5(clock), .in_1(in_4), .in_2(in_3), .in_3(in_2), .in_4(in_1),
    .out_6(register_immediate_output_1_out_6), .out_7(register_immediate_output_1_out_7),
    .out_8(register_immediate_output_1_out_8), .out_9(register_immediate_output_1_out_9));
  and and_3 (out_11, not_2_out, register_immediate_output_2_out_8);
  and and_4 (out_10, not_2_out, register_immediate_output_2_out_7);
  _8_Bit_Adder_main main_1 (
    .in_4(1'b0), .in_5(register_immediate_output_1_out_6), .in_6(register_immediate_output_1_out_7),
    .in_7(register_immediate_output_1_out_8), .in_8(register_immediate_output_1_out_9), .in_9(undriven),
    .in_10(undriven_2), .in_11(undriven_3), .in_12(1'b0), .in_13(counter_1_out_6), .in_14(counter_1_out_5),
    .in_15(counter_1_out_4), .in_16(counter_1_out_3), .out_22(main_1_out_22), .out_23(main_1_out_23),
    .out_24(main_1_out_24), .out_25(main_1_out_25));  // open: in_1, in_2, in_3, Overflow, out_18, out_19, out_20, out_21
  and and_5 (out_12, not_2_out, register_immediate_output_2_out_9);
  counter counter_1 (
    .in_1(n4tick_1tick_1_out_3), .in_2(or_1_out), .out_3(counter_1_out_3), .out_4(counter_1_out_4),
    .out_5(counter_1_out_5), .out_6(counter_1_out_6));
  bz bz_1 (
    .in_9(bz_bnz), .in_4(register_immediate_output_1_out_6), .in_1(register_immediate_output_1_out_7),
    .in_2(register_immediate_output_1_out_8), .in_5(register_immediate_output_1_out_9), .in_6(main_1_out_22),
    .in_7(main_1_out_23), .in_8(main_1_out_24), .in_3(main_1_out_25), .out_10(bz_1_out_10),
    .out_11(bz_1_out_11), .out_12(bz_1_out_12), .out_13(bz_1_out_13));
  register_immediate_output register_immediate_output_2 (
    .in_5(clock), .in_1(bz_1_out_10), .in_2(bz_1_out_11), .in_3(bz_1_out_12), .in_4(bz_1_out_13),
    .out_6(register_immediate_output_2_out_6), .out_7(register_immediate_output_2_out_7),
    .out_8(register_immediate_output_2_out_8), .out_9(register_immediate_output_2_out_9));
endmodule

module counter (
  input  in_1,
  input  in_2,
  output out_3,
  output out_4,
  output out_5,
  output out_6
);

  wire d_ff_1_q, j_k_ff_1_q, j_k_ff_1_qn, j_k_ff_2_q, j_k_ff_2_qn, j_k_ff_3_q, j_k_ff_3_qn, j_k_ff_4_qn;

  D_Flip_Flop d_ff_1 (.clk(in_1), .D(1'b1), .Q(d_ff_1_q), .reset(in_2));  // open: Qn, preset, en
  J_K_Flip_Flop j_k_ff_1 (
    .J(1'b1), .clk(in_1), .K(1'b1), .Q(j_k_ff_1_q), .Qn(j_k_ff_1_qn), .reset(in_2));  // open: preset, en
  J_K_Flip_Flop j_k_ff_2 (
    .J(1'b1), .clk(j_k_ff_1_q), .K(1'b1), .Q(j_k_ff_2_q), .Qn(j_k_ff_2_qn), .reset(in_2));  // open: preset, en
  J_K_Flip_Flop j_k_ff_3 (
    .J(1'b1), .clk(j_k_ff_2_q), .K(1'b1), .Q(j_k_ff_3_q), .Qn(j_k_ff_3_qn), .reset(in_2));  // open: preset, en
  J_K_Flip_Flop j_k_ff_4 (.J(1'b1), .clk(j_k_ff_3_q), .K(1'b1), .Qn(j_k_ff_4_qn), .reset(in_2));  // open: Q, preset, en
  and and_1 (out_3, d_ff_1_q, j_k_ff_1_qn);
  and and_2 (out_4, d_ff_1_q, j_k_ff_2_qn);
  and and_3 (out_5, d_ff_1_q, j_k_ff_3_qn);
  and and_4 (out_6, d_ff_1_q, j_k_ff_4_qn);
endmodule

module register (
  input  in_1,
  input  in_2,
  input  in_3,
  input  in_4,
  input  Clock,
  input  in_6,
  output out_7,
  output out_8,
  output out_9,
  output out_10
);

  D_Flip_Flop d_ff_1 (.clk(Clock), .D(in_1), .Q(out_7));  // open: Qn, preset, en, reset
  D_Flip_Flop d_ff_2 (.clk(Clock), .D(in_2), .Q(out_8), .reset(in_6));  // open: Qn, preset, en
  D_Flip_Flop d_ff_3 (.clk(Clock), .D(in_3), .Q(out_9), .reset(in_6));  // open: Qn, preset, en
  D_Flip_Flop d_ff_4 (.clk(Clock), .D(in_4), .Q(out_10), .reset(in_6));  // open: Qn, preset, en
endmodule

module bz (
  input  in_1,
  input  in_2,
  input  in_3,
  input  in_4,
  input  in_5,
  input  in_6,
  input  in_7,
  input  in_8,
  input  in_9,
  output out_10,
  output out_11,
  output out_12,
  output out_13
);

  wire and_1_out, and_2_out, and_3_out, and_4_out, and_5_out, and_6_out, and_7_out, and_8_out, not_1_out;

  and and_1 (and_1_out, in_1, in_9);
  and and_2 (and_2_out, in_4, in_9);
  and and_3 (and_3_out, in_2, in_9);
  or or_1 (out_10, and_2_out, and_5_out);
  not not_1 (not_1_out, in_9);
  and and_4 (and_4_out, in_5, in_9);
  or or_2 (out_11, and_1_out, and_6_out);
  or or_3 (out_12, and_3_out, and_7_out);
  or or_4 (out_13, and_4_out, and_8_out);
  and and_5 (and_5_out, in_6, not_1_out);
  and and_6 (and_6_out, in_7, not_1_out);
  and and_7 (and_7_out, in_8, not_1_out);
  and and_8 (and_8_out, in_3, not_1_out);
endmodule

module register_immediate_output (
  input  in_1,
  input  in_2,
  input  in_3,
  input  in_4,
  input  in_5,
  output out_6,
  output out_7,
  output out_8,
  output out_9
);

  wire d_ff_1_q, d_ff_2_q, d_ff_3_q, d_ff_4_q, d_ff_5_q, not_1_out, not_2_out, not_3_out, not_4_out;

  not not_1 (not_1_out, in_1);
  D_Flip_Flop d_ff_1 (.Q(d_ff_1_q), .preset(in_1), .reset(not_1_out));  // open: clk, D, Qn, en
  D_Flip_Flop d_ff_2 (.clk(in_5), .D(1'b1), .Q(d_ff_2_q));  // open: Qn, preset, en, reset
  and and_1 (out_6, d_ff_2_q, d_ff_1_q);
  not not_2 (not_2_out, in_2);
  D_Flip_Flop d_ff_3 (.Q(d_ff_3_q), .preset(in_2), .reset(not_2_out));  // open: clk, D, Qn, en
  and and_2 (out_7, d_ff_2_q, d_ff_3_q);
  not not_3 (not_3_out, in_3);
  D_Flip_Flop d_ff_4 (.Q(d_ff_4_q), .preset(in_3), .reset(not_3_out));  // open: clk, D, Qn, en
  and and_3 (out_8, d_ff_2_q, d_ff_4_q);
  not not_4 (not_4_out, in_4);
  D_Flip_Flop d_ff_5 (.Q(d_ff_5_q), .preset(in_4), .reset(not_4_out));  // open: clk, D, Qn, en
  and and_4 (out_9, d_ff_2_q, d_ff_5_q);
endmodule

module _4tick_1tick (
  input  in_1,
  input  in_2,
  output out_3
);

  wire j_k_ff_1_q, j_k_ff_1_qn, j_k_ff_2_qn, not_1_out;

  J_K_Flip_Flop j_k_ff_1 (
    .J(1'b1), .clk(in_1), .K(1'b1), .Q(j_k_ff_1_q), .Qn(j_k_ff_1_qn), .reset(in_2));  // open: preset, en
  J_K_Flip_Flop j_k_ff_2 (.J(1'b1), .clk(j_k_ff_1_q), .K(1'b1), .Qn(j_k_ff_2_qn), .reset(in_2));  // open: Q, preset, en
  not not_1 (not_1_out, j_k_ff_2_qn);
  and and_1 (out_3, j_k_ff_1_qn, not_1_out);
endmodule

module register_saves_data (
  input  in_1,
  input  in_2,
  input  in_3,
  input  in_4,
  input  in_5,
  output out_6,
  output out_7,
  output out_8,
  output out_9
);

  wire d_ff_1_q, d_ff_2_q, d_ff_3_q, d_ff_4_q, d_ff_5_q;

  D_Flip_Flop d_ff_1 (.clk(in_5), .D(in_1), .Q(d_ff_1_q));  // open: Qn, preset, en, reset
  D_Flip_Flop d_ff_2 (.clk(in_5), .D(1'b1), .Q(d_ff_2_q));  // open: Qn, preset, en, reset
  and and_1 (out_6, d_ff_2_q, d_ff_1_q);
  D_Flip_Flop d_ff_3 (.clk(in_5), .D(in_2), .Q(d_ff_3_q));  // open: Qn, preset, en, reset
  and and_2 (out_7, d_ff_2_q, d_ff_3_q);
  D_Flip_Flop d_ff_4 (.clk(in_5), .D(in_3), .Q(d_ff_4_q));  // open: Qn, preset, en, reset
  and and_3 (out_8, d_ff_2_q, d_ff_4_q);
  D_Flip_Flop d_ff_5 (.clk(in_5), .D(in_4), .Q(d_ff_5_q));  // open: Qn, preset, en, reset
  and and_4 (out_9, d_ff_2_q, d_ff_5_q);
endmodule
