// Logisim project bz-bnz analyzer.circ as structural Verilog: 1 circuit, main circuit main
module main (
  input  in_1,
  input  _1_bnz,
  input  in_3,
  input  in_4,
  input  in_5,
  input  in_6,
  input  in_7,
  input  in_8,
  input  in_9,
  input  in_10,
  input  in_11,
  input  in_12,
  input  in_13,
  input  in_14,
  output out_15,
  output out_16,
  output out_17,
  output out_18,
  output success
);

  wire and_1_out, and_2_out, not_1_out, not_2_out, or_1_out;

  not not_1 (not_1_out, or_1_out);
  not not_2 (not_2_out, _1_bnz);
  and and_1 (and_1_out, or_1_out, _1_bnz, in_1);
  or or_1 (or_1_out, in_3, in_4, in_5, in_6, in_7, in_8, in_9, in_10);
  and and_2 (and_2_out, in_1, not_1_out, not_2_out);
  or or_2 (success, and_2_out, and_1_out);
  and and_3 (out_15, in_11, success);
  and and_4 (out_16, in_12, success);
  and and_5 (out_17, in_13, success);
  and and_6 (out_18, in_14, success);

  // Notes on the sheet:
  //   0:bz
  //   R0
  //   0: r0 is zero
  //   address in instruction cache
  //   ready to read from instruction cache
endmodule
