// Logisim project helper.circ as structural Verilog: 1 circuit, main circuit main
module main (
  input  in_1,
  input  in_2,
  input  in_3,
  input  in_4,
  input  in_5,
  input  in_6,
  input  in_7,
  input  in_8,
  input  in_9,
  output out_10,
  output out_11,
  output out_12,
  output out_13
);

  wire and_1_out, and_2_out, and_3_out, and_4_out, and_5_out, and_6_out, and_7_out, and_8_out, not_1_out;

  and and_1 (and_1_out, in_4, in_9);
  and and_2 (and_2_out, in_1, in_9);
  and and_3 (and_3_out, in_2, in_9);
  or or_1 (out_10, and_1_out, and_5_out);
  not not_1 (not_1_out, in_9);
  and and_4 (and_4_out, in_5, in_9);
  or or_2 (out_11, and_2_out, and_6_out);
  or or_3 (out_12, and_3_out, and_7_out);
  or or_4 (out_13, and_4_out, and_8_out);
  and and_5 (and_5_out, in_6, not_1_out);
  and and_6 (and_6_out, in_7, not_1_out);
  and and_7 (and_7_out, in_8, not_1_out);
  and and_8 (and_8_out, in_3, not_1_out);
endmodule
